// Logisim project v0.1.circ as structural Verilog
module rejestr_przerzutnikowy (
  input  in_1,
  input  [7:0] in_2,
  output [7:0] out_3
);

  D_Flip_Flop d_ff_1 (.clk(in_1), .D(in_2[0]), .Q(out_3[0]));  // open: Qn, preset, reset
  D_Flip_Flop d_ff_2 (.clk(in_1), .D(in_2[1]), .Q(out_3[1]));  // open: Qn, preset, reset
  D_Flip_Flop d_ff_3 (.clk(in_1), .D(in_2[2]), .Q(out_3[2]));  // open: Qn, preset, reset
  D_Flip_Flop d_ff_4 (.clk(in_1), .D(in_2[3]), .Q(out_3[3]));  // open: Qn, preset, reset
  D_Flip_Flop d_ff_5 (.clk(in_1), .D(in_2[4]), .Q(out_3[4]));  // open: Qn, preset, reset
  D_Flip_Flop d_ff_6 (.clk(in_1), .D(in_2[5]), .Q(out_3[5]));  // open: Qn, preset, reset
  D_Flip_Flop d_ff_7 (.clk(in_1), .D(in_2[6]), .Q(out_3[6]));  // open: Qn, preset, reset
  D_Flip_Flop d_ff_8 (.clk(in_1), .D(in_2[7]), .Q(out_3[7]));  // open: Qn, preset, reset
endmodule

module Main_Registers (
  input  [15:0] DataIn16,
  input  [7:0] DataIn8,
  input  [1:0] Register16Adr,
  input  [2:0] Register8Adr,
  input  Pair,
  input  Clock,
  input  Reset,
  input  OutSwitch,
  output [15:0] DataOut16,
  output [7:0] DataOut8
);

  wire decoder_1_out0, decoder_1_out1, decoder_1_out2, decoder_1_out3, decoder_1_out4, decoder_1_out5,
       decoder_1_out6, decoder_1_out7, not_1_out;
  wire [7:0] A_q, B_q, C_q, D_q, demultiplexer_2_out0, demultiplexer_2_out1, demultiplexer_2_out2,
       demultiplexer_2_out3, demultiplexer_2_out4, demultiplexer_2_out5, demultiplexer_2_out6,
       demultiplexer_2_out7, E_q, F_q, H_q, L_q, multiplexer_1_out, multiplexer_2_out, multiplexer_3_out,
       multiplexer_4_out, multiplexer_5_out, multiplexer_6_out, multiplexer_7_out, multiplexer_8_out,
       multiplexer_9_out, rozdzielacz16to8_1_out_2, rozdzielacz16to8_1_out_3, rozdzielacz16to8_2_out_2,
       rozdzielacz16to8_2_out_3, rozdzielacz16to8_3_out_2, rozdzielacz16to8_3_out_3,
       rozdzielacz16to8_4_out_2, rozdzielacz16to8_4_out_3;
  wire [15:0] demultiplexer_1_out0, demultiplexer_1_out1, demultiplexer_1_out2, demultiplexer_1_out3,
       multiplexer_10_out, rozdzielac8to16_1_out_3, rozdzielac8to16_2_out_3, rozdzielac8to16_3_out_3,
       rozdzielac8to16_4_out_3;

  rozdzielacz16to8 rozdzielacz16to8_1 (
    .in_1(demultiplexer_1_out0), .out_2(rozdzielacz16to8_1_out_2), .out_3(rozdzielacz16to8_1_out_3));
  Demultiplexer #(.select(2), .width(16)) demultiplexer_1 (
    .out0(demultiplexer_1_out0), .out1(demultiplexer_1_out1), .out2(demultiplexer_1_out2),
    .out3(demultiplexer_1_out3), .in(DataIn16), .sel(Register16Adr));
  rozdzielacz16to8 rozdzielacz16to8_2 (
    .in_1(demultiplexer_1_out1), .out_2(rozdzielacz16to8_2_out_2), .out_3(rozdzielacz16to8_2_out_3));
  rozdzielacz16to8 rozdzielacz16to8_3 (
    .in_1(demultiplexer_1_out2), .out_2(rozdzielacz16to8_3_out_2), .out_3(rozdzielacz16to8_3_out_3));
  rozdzielacz16to8 rozdzielacz16to8_4 (
    .in_1(demultiplexer_1_out3), .out_2(rozdzielacz16to8_4_out_2), .out_3(rozdzielacz16to8_4_out_3));
  Demultiplexer #(.select(3), .width(8)) demultiplexer_2 (
    .out0(demultiplexer_2_out0), .out1(demultiplexer_2_out1), .out2(demultiplexer_2_out2),
    .out3(demultiplexer_2_out3), .out4(demultiplexer_2_out4), .out5(demultiplexer_2_out5),
    .out6(demultiplexer_2_out6), .out7(demultiplexer_2_out7), .in(DataIn8), .sel(Register8Adr));
  Decoder #(.select(3)) decoder_1 (
    .out0(decoder_1_out0), .out1(decoder_1_out1), .out2(decoder_1_out2), .out3(decoder_1_out3),
    .out4(decoder_1_out4), .out5(decoder_1_out5), .out6(decoder_1_out6), .out7(decoder_1_out7),
    .sel(Register8Adr), .en(not_1_out));
  not not_1 (not_1_out, Pair);
  Multiplexer #(.width(8)) multiplexer_1 (
    .in0(rozdzielacz16to8_1_out_2), .in1(demultiplexer_2_out0), .out(multiplexer_1_out), .sel(Pair));
  Multiplexer #(.width(8)) multiplexer_2 (
    .in0(rozdzielacz16to8_2_out_2), .in1(demultiplexer_2_out1), .out(multiplexer_2_out), .sel(Pair));
  Multiplexer #(.width(8)) multiplexer_3 (
    .in0(rozdzielacz16to8_3_out_2), .in1(demultiplexer_2_out2), .out(multiplexer_3_out), .sel(Pair));
  Multiplexer #(.width(8)) multiplexer_4 (
    .in0(rozdzielacz16to8_4_out_2), .in1(demultiplexer_2_out3), .out(multiplexer_4_out), .sel(Pair));
  Multiplexer #(.width(8)) multiplexer_5 (
    .in0(rozdzielacz16to8_1_out_3), .in1(demultiplexer_2_out4), .out(multiplexer_5_out), .sel(Pair));
  Multiplexer #(.width(8)) multiplexer_6 (
    .in0(rozdzielacz16to8_2_out_3), .in1(demultiplexer_2_out5), .out(multiplexer_6_out), .sel(Pair));
  Multiplexer #(.width(8)) multiplexer_7 (
    .in0(rozdzielacz16to8_3_out_3), .in1(demultiplexer_2_out6), .out(multiplexer_7_out), .sel(Pair));
  Multiplexer #(.width(8)) multiplexer_8 (
    .in0(rozdzielacz16to8_4_out_3), .in1(demultiplexer_2_out7), .out(multiplexer_8_out), .sel(Pair));
  Register A (.D(multiplexer_1_out), .en(decoder_1_out7), .clk(Clock), .Q(A_q), .clr(Reset));
  Register B (.D(multiplexer_2_out), .en(decoder_1_out6), .clk(Clock), .Q(B_q), .clr(Reset));
  Register D (.D(multiplexer_3_out), .en(decoder_1_out5), .clk(Clock), .Q(D_q), .clr(Reset));
  Register H (.D(multiplexer_4_out), .en(decoder_1_out4), .clk(Clock), .Q(H_q), .clr(Reset));
  Register F (.D(multiplexer_5_out), .en(decoder_1_out3), .clk(Clock), .Q(F_q), .clr(Reset));
  Register C (.D(multiplexer_6_out), .en(decoder_1_out2), .clk(Clock), .Q(C_q), .clr(Reset));
  Register E (.D(multiplexer_7_out), .en(decoder_1_out1), .clk(Clock), .Q(E_q), .clr(Reset));
  Register L (.D(multiplexer_8_out), .en(decoder_1_out0), .clk(Clock), .Q(L_q), .clr(Reset));
  rozdzielac8to16 rozdzielac8to16_1 (.in_1(F_q), .in_2(A_q), .out_3(rozdzielac8to16_1_out_3));
  rozdzielac8to16 rozdzielac8to16_2 (.in_1(C_q), .in_2(B_q), .out_3(rozdzielac8to16_2_out_3));
  rozdzielac8to16 rozdzielac8to16_3 (.in_1(E_q), .in_2(D_q), .out_3(rozdzielac8to16_3_out_3));
  rozdzielac8to16 rozdzielac8to16_4 (.in_1(L_q), .in_2(H_q), .out_3(rozdzielac8to16_4_out_3));
  Multiplexer #(.select(3), .width(8)) multiplexer_9 (
    .in0(A_q), .in1(B_q), .in2(D_q), .in3(H_q), .in4(F_q), .in5(C_q), .in6(E_q), .in7(L_q),
    .out(multiplexer_9_out), .sel(Register8Adr));
  Pull_Resistor pull_resistor_1 (.node(DataOut16));
  assign DataOut16 = OutSwitch ? multiplexer_10_out : 16'bz;  // Controlled_Buffer controlled_buffer_1
  Multiplexer #(.select(2), .width(16)) multiplexer_10 (
    .in0(rozdzielac8to16_1_out_3), .in1(rozdzielac8to16_2_out_3), .in2(rozdzielac8to16_3_out_3),
    .in3(rozdzielac8to16_4_out_3), .out(multiplexer_10_out), .sel(Register16Adr));
  Pull_Resistor pull_resistor_2 (.node(DataOut8));
  assign DataOut8 = OutSwitch ? multiplexer_9_out : 8'bz;  // Controlled_Buffer controlled_buffer_2
endmodule

module rozdzielac8to16 (
  input  [7:0] in_1,
  input  [7:0] in_2,
  output [15:0] out_3
);


  assign out_3 = {in_2, in_1};
endmodule

module rozdzielacz16to8 (
  input  [15:0] in_1,
  output [7:0] out_2,
  output [7:0] out_3
);


  assign out_2 = in_1[7:0];
  assign out_3 = in_1[15:8];
endmodule

module akumulatorsum (
  input  [7:0] INDATA,
  input  in_2,
  input  CLK,
  output [7:0] OUTDATA,
  output FCER
);

  wire [7:0] adder_1_out;

  Register register_1 (.D(adder_1_out), .en(in_2), .clk(CLK), .Q(OUTDATA));  // open: clr
  Adder adder_1 (.a(OUTDATA), .b(INDATA), .out(adder_1_out), .cout(FCER));  // open: cin
endmodule

module rejestrindeks (
  input  [15:0] INDATA,
  input  [1:0] AD,
  input  W,
  input  CLK,
  input  RES,
  input  LD,
  output [15:0] OUTDATA
);

  wire decoder_1_out0, decoder_1_out1, decoder_1_out2;
  wire [15:0] demultiplexer_1_out0, demultiplexer_1_out1, demultiplexer_1_out2, IX_q, IY_q,
       multiplexer_1_out, SP_q;

  Decoder #(.select(2)) decoder_1 (
    .out0(decoder_1_out0), .out1(decoder_1_out1), .out2(decoder_1_out2), .sel(AD), .en(W));  // open: out3
  Demultiplexer #(.select(2), .width(16)) demultiplexer_1 (
    .out0(demultiplexer_1_out0), .out1(demultiplexer_1_out1), .out2(demultiplexer_1_out2), .in(INDATA),
    .sel(AD));  // open: out3
  Register #(.width(16)) IX (.D(demultiplexer_1_out0), .en(decoder_1_out0), .clk(CLK), .Q(IX_q), .clr(RES));
  Register #(.width(16)) IY (.D(demultiplexer_1_out1), .en(decoder_1_out1), .clk(CLK), .Q(IY_q), .clr(RES));
  Register #(.width(16)) SP (.D(demultiplexer_1_out2), .en(decoder_1_out2), .clk(CLK), .Q(SP_q), .clr(RES));
  Multiplexer #(.select(2), .width(16)) multiplexer_1 (
    .in0(IX_q), .in1(IY_q), .in2(SP_q), .out(multiplexer_1_out), .sel(AD));  // open: in3
  Pull_Resistor pull_resistor_1 (.node(OUTDATA));
  assign OUTDATA = LD ? multiplexer_1_out : 16'bz;  // Controlled_Buffer controlled_buffer_1
endmodule
