// Logisim project v0.12.circ as structural Verilog
module rejestr_przerzutnikowy (
  input  in_1,
  input  [7:0] in_2,
  output [7:0] out_3
);

  D_Flip_Flop d_ff_1 (.clk(in_1), .D(in_2[0]), .Q(out_3[0]));  // open: Qn, preset, reset
  D_Flip_Flop d_ff_2 (.clk(in_1), .D(in_2[1]), .Q(out_3[1]));  // open: Qn, preset, reset
  D_Flip_Flop d_ff_3 (.clk(in_1), .D(in_2[2]), .Q(out_3[2]));  // open: Qn, preset, reset
  D_Flip_Flop d_ff_4 (.clk(in_1), .D(in_2[3]), .Q(out_3[3]));  // open: Qn, preset, reset
  D_Flip_Flop d_ff_5 (.clk(in_1), .D(in_2[4]), .Q(out_3[4]));  // open: Qn, preset, reset
  D_Flip_Flop d_ff_6 (.clk(in_1), .D(in_2[5]), .Q(out_3[5]));  // open: Qn, preset, reset
  D_Flip_Flop d_ff_7 (.clk(in_1), .D(in_2[6]), .Q(out_3[6]));  // open: Qn, preset, reset
  D_Flip_Flop d_ff_8 (.clk(in_1), .D(in_2[7]), .Q(out_3[7]));  // open: Qn, preset, reset
endmodule

module Main_Registers (
  input  [15:0] DataIn16,
  input  [7:0] DataIn8,
  input  [1:0] Address16,
  input  [2:0] Address8,
  input  Pair,
  input  Clock,
  input  Reset,
  input  OutSwitch,
  output [15:0] DataOut16,
  output [7:0] DataOut8
);

  wire and_1_out, decoder_1_out0, decoder_1_out1, decoder_1_out2, decoder_1_out3, decoder_1_out4,
       decoder_1_out5, decoder_1_out6, decoder_1_out7, demultiplexer_3_out0, demultiplexer_3_out1,
       demultiplexer_3_out2, demultiplexer_3_out3, not_1_out, or_1_out, or_2_out, or_3_out, or_4_out,
       or_5_out, or_6_out, or_7_out, or_8_out, xor_1_out;
  wire [7:0] B_q, C_q, D_q, demultiplexer_2_out0, demultiplexer_2_out1, demultiplexer_2_out2,
       demultiplexer_2_out3, demultiplexer_2_out4, demultiplexer_2_out5, demultiplexer_2_out6,
       demultiplexer_2_out7, E_q, H_q, L_q, multiplexer_1_out, multiplexer_2_out, multiplexer_3_out,
       multiplexer_4_out, multiplexer_5_out, multiplexer_6_out, multiplexer_7_out, multiplexer_8_out,
       multiplexer_10_out, rozdzielacz16to8_1_out_2, rozdzielacz16to8_1_out_3, rozdzielacz16to8_2_out_2,
       rozdzielacz16to8_2_out_3, rozdzielacz16to8_3_out_2, rozdzielacz16to8_3_out_3,
       rozdzielacz16to8_4_out_2, rozdzielacz16to8_4_out_3, W_q, Z_q;
  wire [15:0] demultiplexer_1_out0, demultiplexer_1_out1, demultiplexer_1_out2, demultiplexer_1_out3,
       multiplexer_9_out, rozdzielac8to16_1_out_3, rozdzielac8to16_2_out_3, rozdzielac8to16_3_out_3,
       rozdzielac8to16_4_out_3;

  rozdzielacz16to8 rozdzielacz16to8_1 (
    .in_1(demultiplexer_1_out0), .out_2(rozdzielacz16to8_1_out_2), .out_3(rozdzielacz16to8_1_out_3));
  rozdzielacz16to8 rozdzielacz16to8_2 (
    .in_1(demultiplexer_1_out1), .out_2(rozdzielacz16to8_2_out_2), .out_3(rozdzielacz16to8_2_out_3));
  Demultiplexer #(.select(2), .width(16)) demultiplexer_1 (
    .out0(demultiplexer_1_out0), .out1(demultiplexer_1_out1), .out2(demultiplexer_1_out2),
    .out3(demultiplexer_1_out3), .in(DataIn16), .sel(Address16));
  rozdzielacz16to8 rozdzielacz16to8_3 (
    .in_1(demultiplexer_1_out2), .out_2(rozdzielacz16to8_3_out_2), .out_3(rozdzielacz16to8_3_out_3));
  rozdzielacz16to8 rozdzielacz16to8_4 (
    .in_1(demultiplexer_1_out3), .out_2(rozdzielacz16to8_4_out_2), .out_3(rozdzielacz16to8_4_out_3));
  Demultiplexer #(.select(3), .width(8)) demultiplexer_2 (
    .out0(demultiplexer_2_out0), .out1(demultiplexer_2_out1), .out2(demultiplexer_2_out2),
    .out3(demultiplexer_2_out3), .out4(demultiplexer_2_out4), .out5(demultiplexer_2_out5),
    .out6(demultiplexer_2_out6), .out7(demultiplexer_2_out7), .in(DataIn8), .sel(Address8));
  Decoder #(.select(3)) decoder_1 (
    .out0(decoder_1_out0), .out1(decoder_1_out1), .out2(decoder_1_out2), .out3(decoder_1_out3),
    .out4(decoder_1_out4), .out5(decoder_1_out5), .out6(decoder_1_out6), .out7(decoder_1_out7),
    .sel(Address8), .en(not_1_out));
  not not_1 (not_1_out, Pair);
  Multiplexer #(.width(8)) multiplexer_1 (
    .in0(demultiplexer_2_out0), .in1(rozdzielacz16to8_1_out_2), .out(multiplexer_1_out), .sel(Pair));
  Multiplexer #(.width(8)) multiplexer_2 (
    .in0(demultiplexer_2_out1), .in1(rozdzielacz16to8_2_out_2), .out(multiplexer_2_out), .sel(Pair));
  Multiplexer #(.width(8)) multiplexer_3 (
    .in0(demultiplexer_2_out2), .in1(rozdzielacz16to8_3_out_2), .out(multiplexer_3_out), .sel(Pair));
  Multiplexer #(.width(8)) multiplexer_4 (
    .in0(demultiplexer_2_out3), .in1(rozdzielacz16to8_4_out_2), .out(multiplexer_4_out), .sel(Pair));
  Multiplexer #(.width(8)) multiplexer_5 (
    .in0(demultiplexer_2_out4), .in1(rozdzielacz16to8_1_out_3), .out(multiplexer_5_out), .sel(Pair));
  Multiplexer #(.width(8)) multiplexer_6 (
    .in0(demultiplexer_2_out5), .in1(rozdzielacz16to8_2_out_3), .out(multiplexer_6_out), .sel(Pair));
  Multiplexer #(.width(8)) multiplexer_7 (
    .in0(demultiplexer_2_out6), .in1(rozdzielacz16to8_3_out_3), .out(multiplexer_7_out), .sel(Pair));
  Multiplexer #(.width(8)) multiplexer_8 (
    .in0(demultiplexer_2_out7), .in1(rozdzielacz16to8_4_out_3), .out(multiplexer_8_out), .sel(Pair));
  Demultiplexer #(.select(2)) demultiplexer_3 (
    .out0(demultiplexer_3_out0), .out1(demultiplexer_3_out1), .out2(demultiplexer_3_out2),
    .out3(demultiplexer_3_out3), .in(Pair), .sel(Address16));
  Register W (.D(multiplexer_1_out), .en(or_1_out), .clk(Clock), .Q(W_q), .clr(Reset));
  or or_1 (or_1_out, decoder_1_out0, demultiplexer_3_out0);
  Register B (.D(multiplexer_2_out), .en(or_2_out), .clk(Clock), .Q(B_q), .clr(Reset));
  or or_2 (or_2_out, decoder_1_out1, demultiplexer_3_out1);
  Register D (.D(multiplexer_3_out), .en(or_3_out), .clk(Clock), .Q(D_q), .clr(Reset));
  or or_3 (or_3_out, decoder_1_out2, demultiplexer_3_out2);
  Register H (.D(multiplexer_4_out), .en(or_4_out), .clk(Clock), .Q(H_q), .clr(Reset));
  or or_4 (or_4_out, decoder_1_out3, demultiplexer_3_out3);
  Register Z (.D(multiplexer_5_out), .en(or_5_out), .clk(Clock), .Q(Z_q), .clr(Reset));
  or or_5 (or_5_out, decoder_1_out4, demultiplexer_3_out0);
  Register C (.D(multiplexer_6_out), .en(or_6_out), .clk(Clock), .Q(C_q), .clr(Reset));
  or or_6 (or_6_out, decoder_1_out5, demultiplexer_3_out1);
  Register E (.D(multiplexer_7_out), .en(or_7_out), .clk(Clock), .Q(E_q), .clr(Reset));
  or or_7 (or_7_out, decoder_1_out6, demultiplexer_3_out2);
  Register L (.D(multiplexer_8_out), .en(or_8_out), .clk(Clock), .Q(L_q), .clr(Reset));
  or or_8 (or_8_out, decoder_1_out7, demultiplexer_3_out3);
  rozdzielac8to16 rozdzielac8to16_1 (.in_1(Z_q), .in_2(W_q), .out_3(rozdzielac8to16_1_out_3));
  rozdzielac8to16 rozdzielac8to16_2 (.in_1(C_q), .in_2(B_q), .out_3(rozdzielac8to16_2_out_3));
  rozdzielac8to16 rozdzielac8to16_3 (.in_1(E_q), .in_2(D_q), .out_3(rozdzielac8to16_3_out_3));
  rozdzielac8to16 rozdzielac8to16_4 (.in_1(L_q), .in_2(H_q), .out_3(rozdzielac8to16_4_out_3));
  Multiplexer #(.select(2), .width(16)) multiplexer_9 (
    .in0(rozdzielac8to16_1_out_3), .in1(rozdzielac8to16_2_out_3), .in2(rozdzielac8to16_3_out_3),
    .in3(rozdzielac8to16_4_out_3), .out(multiplexer_9_out), .sel(Address16));
  assign DataOut8 = xor_1_out ? multiplexer_10_out : 8'bz;  // Controlled_Buffer controlled_buffer_1
  Multiplexer #(.select(3), .width(8)) multiplexer_10 (
    .in0(W_q), .in1(B_q), .in2(D_q), .in3(H_q), .in4(Z_q), .in5(C_q), .in6(E_q), .in7(L_q),
    .out(multiplexer_10_out), .sel(Address8));
  xor xor_1 (xor_1_out, Pair, OutSwitch);
  Pull_Resistor pull_resistor_1 (.node(DataOut16));
  assign DataOut16 = and_1_out ? multiplexer_9_out : 16'bz;  // Controlled_Buffer controlled_buffer_2
  Pull_Resistor pull_resistor_2 (.node(DataOut8));
  and and_1 (and_1_out, OutSwitch, Pair);
endmodule

module rozdzielac8to16 (
  input  [7:0] in_1,
  input  [7:0] in_2,
  output [15:0] out_3
);


  assign out_3 = {in_2, in_1};
endmodule

module rozdzielacz16to8 (
  input  [15:0] in_1,
  output [7:0] out_2,
  output [7:0] out_3
);


  assign out_2 = in_1[7:0];
  assign out_3 = in_1[15:8];
endmodule

module akumulatorsum (
  input  [7:0] INDATA,
  input  in_2,
  input  CLK,
  output [7:0] OUTDATA,
  output FCER
);

  wire [7:0] adder_1_out;

  Register register_1 (.D(adder_1_out), .en(in_2), .clk(CLK), .Q(OUTDATA));  // open: clr
  Adder adder_1 (.a(OUTDATA), .b(INDATA), .out(adder_1_out), .cout(FCER));  // open: cin
endmodule

module Registers16 (
  input  [1:0] Address,
  input  [15:0] DataIn,
  input  Clock,
  input  Reset,
  input  OutSwitch,
  output [15:0] DataOut
);

  wire demultiplexer_2_out0, demultiplexer_2_out1, demultiplexer_2_out2;
  wire [15:0] demultiplexer_1_out0, demultiplexer_1_out1, demultiplexer_1_out2, IX_q, IY_q,
       multiplexer_1_out, SP_q;

  Demultiplexer #(.select(2), .width(16)) demultiplexer_1 (
    .out0(demultiplexer_1_out0), .out1(demultiplexer_1_out1), .out2(demultiplexer_1_out2), .in(DataIn),
    .sel(Address));  // open: out3
  Demultiplexer #(.select(2)) demultiplexer_2 (
    .out0(demultiplexer_2_out0), .out1(demultiplexer_2_out1), .out2(demultiplexer_2_out2), .sel(Address));  // open: out3, in
  Register #(.width(16)) IX (.D(demultiplexer_1_out0), .en(demultiplexer_2_out0), .clk(Clock), .Q(IX_q), .clr(Reset));
  Register #(.width(16)) IY (.D(demultiplexer_1_out1), .en(demultiplexer_2_out1), .clk(Clock), .Q(IY_q), .clr(Reset));
  Register #(.width(16)) SP (.D(demultiplexer_1_out2), .en(demultiplexer_2_out2), .clk(Clock), .Q(SP_q), .clr(Reset));
  assign DataOut = OutSwitch ? multiplexer_1_out : 16'bz;  // Controlled_Buffer controlled_buffer_1
  Multiplexer #(.select(2), .width(16)) multiplexer_1 (
    .in0(IX_q), .in1(IY_q), .in2(SP_q), .out(multiplexer_1_out));  // open: in3, sel
  Pull_Resistor pull_resistor_1 (.node(DataOut));
endmodule

module ALU (
  input  [7:0] In1,
  input  [7:0] In2
);

  wire adder_1_cout, undriven, undriven_2, undriven_3, undriven_4, undriven_5, undriven_6, undriven_7,
       undriven_8, undriven_9, undriven_10, undriven_11, undriven_12, undriven_13;
  wire [0:0] pull_resistor_2_node;
  wire [7:0] controlled_buffer_1_out, controlled_buffer_2_out, controlled_buffer_3_out,
       controlled_buffer_4_out, controlled_buffer_5_out, controlled_buffer_6_out, controlled_buffer_7_out,
       controlled_buffer_8_out, controlled_buffer_9_out, controlled_buffer_10_out, controlled_buffer_11_out,
       controlled_buffer_12_out, controlled_buffer_13_out, controlled_buffer_14_out,
       controlled_buffer_15_out, controlled_buffer_16_out, controlled_buffer_17_out,
       controlled_buffer_18_out, inkrementacja_1_dataout;
  wire [7:7] pull_resistor_1_node;

  assign controlled_buffer_1_out = undriven ? In1 : 8'bz;  // Controlled_Buffer controlled_buffer_1
  assign controlled_buffer_2_out = undriven ? In2 : 8'bz;  // Controlled_Buffer controlled_buffer_2
  assign controlled_buffer_3_out = undriven_2 ? In1 : 8'bz;  // Controlled_Buffer controlled_buffer_3
  assign controlled_buffer_4_out = undriven_2 ? In2 : 8'bz;  // Controlled_Buffer controlled_buffer_4
  assign controlled_buffer_5_out = undriven_3 ? In1 : 8'bz;  // Controlled_Buffer controlled_buffer_5
  assign controlled_buffer_6_out = undriven_3 ? In2 : 8'bz;  // Controlled_Buffer controlled_buffer_6
  assign controlled_buffer_7_out = undriven_4 ? In1 : 8'bz;  // Controlled_Buffer controlled_buffer_7
  assign controlled_buffer_8_out = undriven_4 ? In2 : 8'bz;  // Controlled_Buffer controlled_buffer_8
  assign controlled_buffer_9_out = undriven_5 ? In1 : 8'bz;  // Controlled_Buffer controlled_buffer_9
  assign controlled_buffer_10_out = undriven_5 ? In2 : 8'bz;  // Controlled_Buffer controlled_buffer_10
  assign controlled_buffer_11_out = undriven_6 ? In1 : 8'bz;  // Controlled_Buffer controlled_buffer_11
  assign controlled_buffer_12_out = undriven_6 ? In2 : 8'bz;  // Controlled_Buffer controlled_buffer_12
  assign controlled_buffer_13_out = undriven_7 ? In1 : 8'bz;  // Controlled_Buffer controlled_buffer_13
  assign controlled_buffer_14_out = undriven_8 ? In1 : 8'bz;  // Controlled_Buffer controlled_buffer_14
  Pull_Resistor pull_resistor_1 (.node(pull_resistor_1_node[7]));
  assign controlled_buffer_15_out = undriven_9 ? In1 : 8'bz;  // Controlled_Buffer controlled_buffer_15
  assign controlled_buffer_16_out = undriven_10 ? In1 : 8'bz;  // Controlled_Buffer controlled_buffer_16
  assign controlled_buffer_17_out = undriven_11 ? In1 : 8'bz;  // Controlled_Buffer controlled_buffer_17
  assign controlled_buffer_18_out = undriven_12 ? In1 : 8'bz;  // Controlled_Buffer controlled_buffer_18
  inkrementacja inkrementacja_1 (.DataIn(controlled_buffer_18_out), .DataOut(inkrementacja_1_dataout));  // open: Carry
  Adder adder_1 (
    .a(controlled_buffer_1_out), .b(controlled_buffer_2_out), .cin(undriven_13), .cout(adder_1_cout));  // open: out
  Subtractor subtractor_1 (
    .a(controlled_buffer_3_out), .b(controlled_buffer_4_out), .bin(undriven_13), .bout(adder_1_cout));  // open: out
  // AND_Gate and_1 has open pins: in0=controlled_buffer_5_out, in1=controlled_buffer_6_out, out=open
  // OR_Gate or_1 has open pins: in0=controlled_buffer_7_out, in1=controlled_buffer_8_out, out=open
  // XOR_Gate xor_1 has open pins: in0=controlled_buffer_9_out, in1=controlled_buffer_10_out, out=open
  Comparator #(.mode("unsigned")) comparator_1 (
    .a(controlled_buffer_11_out), .b(controlled_buffer_12_out));  // open: gt, eq, lt
  Pull_Resistor pull_resistor_2 (.node(pull_resistor_2_node[0]));
endmodule

module inkrementacja (
  input  [7:0] DataIn,
  output [7:0] DataOut,
  output Carry
);

  wire and_1_out, and_2_out, and_3_out, and_4_out, and_5_out, and_6_out, and_7_out;

  xor xor_1 (DataOut[0], 1'b1, DataIn[0]);
  and and_1 (and_1_out, 1'b1, DataIn[0]);
  xor xor_2 (DataOut[1], and_1_out, DataIn[1]);
  and and_2 (and_2_out, and_1_out, DataIn[1]);
  xor xor_3 (DataOut[2], and_2_out, DataIn[2]);
  and and_3 (and_3_out, and_2_out, DataIn[2]);
  xor xor_4 (DataOut[3], and_3_out, DataIn[3]);
  and and_4 (and_4_out, and_3_out, DataIn[3]);
  xor xor_5 (DataOut[4], and_4_out, DataIn[4]);
  and and_5 (and_5_out, and_4_out, DataIn[4]);
  xor xor_6 (DataOut[5], and_5_out, DataIn[5]);
  and and_6 (and_6_out, and_5_out, DataIn[5]);
  xor xor_7 (DataOut[6], and_6_out, DataIn[6]);
  and and_7 (and_7_out, and_6_out, DataIn[6]);
  xor xor_8 (DataOut[7], and_7_out, DataIn[7]);
  and and_8 (Carry, and_7_out, DataIn[7]);
endmodule
