// Logisim project v0.2.circ as structural Verilog
module main (
  input  [7:0] in_1,
  input  in_2,
  input  in_3,
  input  [7:0] in_4,
  input  [2:0] in_5,
  input  in_6,
  input  in_7,
  input  in_8,
  input  in_9,
  input  [2:0] in_10,
  input  [4:0] in_11,
  output [7:0] out_12,
  output [7:0] out_13
);

  wire [7:0] main_registers_1_dataout8, or_1_out, register_1_q;

  assign or_1_out = in_1 | out_13;  // OR_Gate or_1, 8 bits wide
  Register register_1 (.D(or_1_out), .en(in_2), .clk(in_3), .Q(register_1_q));  // open: clr
  // Registers16 registers16_1: pin names not known
  Main_Registers main_registers_1 (
    .DataIn8(in_4), .Address8(in_5), .Clock(in_6), .Reset(in_7), .OutSwitch(in_8),
    .DataOut8(main_registers_1_dataout8));  // open: DataIn16, Address16, Pair, DataOut16
  ALU alu_1 (
    .DataIn1(register_1_q), .DataIn2(main_registers_1_dataout8), .InstAddr(in_11), .SwitchOut(in_9),
    .BitAddr(in_10), .FlagsOut(out_12), .DataOut(out_13));  // open: FlagsIn
endmodule

module rejestr_przerzutnikowy (
  input  in_1,
  input  [7:0] in_2,
  output [7:0] out_3
);

  D_Flip_Flop d_ff_1 (.clk(in_1), .D(in_2[0]), .Q(out_3[0]));  // open: Qn, preset, reset
  D_Flip_Flop d_ff_2 (.clk(in_1), .D(in_2[1]), .Q(out_3[1]));  // open: Qn, preset, reset
  D_Flip_Flop d_ff_3 (.clk(in_1), .D(in_2[2]), .Q(out_3[2]));  // open: Qn, preset, reset
  D_Flip_Flop d_ff_4 (.clk(in_1), .D(in_2[3]), .Q(out_3[3]));  // open: Qn, preset, reset
  D_Flip_Flop d_ff_5 (.clk(in_1), .D(in_2[4]), .Q(out_3[4]));  // open: Qn, preset, reset
  D_Flip_Flop d_ff_6 (.clk(in_1), .D(in_2[5]), .Q(out_3[5]));  // open: Qn, preset, reset
  D_Flip_Flop d_ff_7 (.clk(in_1), .D(in_2[6]), .Q(out_3[6]));  // open: Qn, preset, reset
  D_Flip_Flop d_ff_8 (.clk(in_1), .D(in_2[7]), .Q(out_3[7]));  // open: Qn, preset, reset
endmodule

module Main_Registers (
  input  [15:0] DataIn16,
  input  [7:0] DataIn8,
  input  [1:0] Address16,
  input  [2:0] Address8,
  input  Pair,
  input  Clock,
  input  Reset,
  input  OutSwitch,
  output [15:0] DataOut16,
  output [7:0] DataOut8
);

  wire and_1_out, decoder_1_out0, decoder_1_out1, decoder_1_out2, decoder_1_out3, decoder_1_out4,
       decoder_1_out5, decoder_1_out6, decoder_1_out7, demultiplexer_3_out0, demultiplexer_3_out1,
       demultiplexer_3_out2, demultiplexer_3_out3, not_1_out, or_1_out, or_2_out, or_3_out, or_4_out,
       or_5_out, or_6_out, or_7_out, or_8_out, xor_1_out;
  wire [7:0] B_q, C_q, D_q, demultiplexer_2_out0, demultiplexer_2_out1, demultiplexer_2_out2,
       demultiplexer_2_out3, demultiplexer_2_out4, demultiplexer_2_out5, demultiplexer_2_out6,
       demultiplexer_2_out7, E_q, H_q, L_q, multiplexer_1_out, multiplexer_2_out, multiplexer_3_out,
       multiplexer_4_out, multiplexer_5_out, multiplexer_6_out, multiplexer_7_out, multiplexer_8_out,
       multiplexer_10_out, rozdzielacz16to8_1_out_2, rozdzielacz16to8_1_out_3, rozdzielacz16to8_2_out_2,
       rozdzielacz16to8_2_out_3, rozdzielacz16to8_3_out_2, rozdzielacz16to8_3_out_3,
       rozdzielacz16to8_4_out_2, rozdzielacz16to8_4_out_3, W_q, Z_q;
  wire [15:0] demultiplexer_1_out0, demultiplexer_1_out1, demultiplexer_1_out2, demultiplexer_1_out3,
       multiplexer_9_out, rozdzielac8to16_1_out_3, rozdzielac8to16_2_out_3, rozdzielac8to16_3_out_3,
       rozdzielac8to16_4_out_3;

  rozdzielacz16to8 rozdzielacz16to8_1 (
    .in_1(demultiplexer_1_out0), .out_2(rozdzielacz16to8_1_out_2), .out_3(rozdzielacz16to8_1_out_3));
  rozdzielacz16to8 rozdzielacz16to8_2 (
    .in_1(demultiplexer_1_out1), .out_2(rozdzielacz16to8_2_out_2), .out_3(rozdzielacz16to8_2_out_3));
  Demultiplexer #(.select(2), .width(16)) demultiplexer_1 (
    .out0(demultiplexer_1_out0), .out1(demultiplexer_1_out1), .out2(demultiplexer_1_out2),
    .out3(demultiplexer_1_out3), .in(DataIn16), .sel(Address16));
  rozdzielacz16to8 rozdzielacz16to8_3 (
    .in_1(demultiplexer_1_out2), .out_2(rozdzielacz16to8_3_out_2), .out_3(rozdzielacz16to8_3_out_3));
  rozdzielacz16to8 rozdzielacz16to8_4 (
    .in_1(demultiplexer_1_out3), .out_2(rozdzielacz16to8_4_out_2), .out_3(rozdzielacz16to8_4_out_3));
  Demultiplexer #(.select(3), .width(8)) demultiplexer_2 (
    .out0(demultiplexer_2_out0), .out1(demultiplexer_2_out1), .out2(demultiplexer_2_out2),
    .out3(demultiplexer_2_out3), .out4(demultiplexer_2_out4), .out5(demultiplexer_2_out5),
    .out6(demultiplexer_2_out6), .out7(demultiplexer_2_out7), .in(DataIn8), .sel(Address8));
  Decoder #(.select(3)) decoder_1 (
    .out0(decoder_1_out0), .out1(decoder_1_out1), .out2(decoder_1_out2), .out3(decoder_1_out3),
    .out4(decoder_1_out4), .out5(decoder_1_out5), .out6(decoder_1_out6), .out7(decoder_1_out7),
    .sel(Address8), .en(not_1_out));
  not not_1 (not_1_out, Pair);
  Multiplexer #(.width(8)) multiplexer_1 (
    .in0(demultiplexer_2_out0), .in1(rozdzielacz16to8_1_out_2), .out(multiplexer_1_out), .sel(Pair));
  Multiplexer #(.width(8)) multiplexer_2 (
    .in0(demultiplexer_2_out1), .in1(rozdzielacz16to8_2_out_2), .out(multiplexer_2_out), .sel(Pair));
  Multiplexer #(.width(8)) multiplexer_3 (
    .in0(demultiplexer_2_out2), .in1(rozdzielacz16to8_3_out_2), .out(multiplexer_3_out), .sel(Pair));
  Multiplexer #(.width(8)) multiplexer_4 (
    .in0(demultiplexer_2_out3), .in1(rozdzielacz16to8_4_out_2), .out(multiplexer_4_out), .sel(Pair));
  Multiplexer #(.width(8)) multiplexer_5 (
    .in0(demultiplexer_2_out4), .in1(rozdzielacz16to8_1_out_3), .out(multiplexer_5_out), .sel(Pair));
  Multiplexer #(.width(8)) multiplexer_6 (
    .in0(demultiplexer_2_out5), .in1(rozdzielacz16to8_2_out_3), .out(multiplexer_6_out), .sel(Pair));
  Multiplexer #(.width(8)) multiplexer_7 (
    .in0(demultiplexer_2_out6), .in1(rozdzielacz16to8_3_out_3), .out(multiplexer_7_out), .sel(Pair));
  Multiplexer #(.width(8)) multiplexer_8 (
    .in0(demultiplexer_2_out7), .in1(rozdzielacz16to8_4_out_3), .out(multiplexer_8_out), .sel(Pair));
  Demultiplexer #(.select(2)) demultiplexer_3 (
    .out0(demultiplexer_3_out0), .out1(demultiplexer_3_out1), .out2(demultiplexer_3_out2),
    .out3(demultiplexer_3_out3), .in(Pair), .sel(Address16));
  Register W (.D(multiplexer_1_out), .en(or_1_out), .clk(Clock), .Q(W_q), .clr(Reset));
  or or_1 (or_1_out, decoder_1_out0, demultiplexer_3_out0);
  Register B (.D(multiplexer_2_out), .en(or_2_out), .clk(Clock), .Q(B_q), .clr(Reset));
  or or_2 (or_2_out, decoder_1_out1, demultiplexer_3_out1);
  Register D (.D(multiplexer_3_out), .en(or_3_out), .clk(Clock), .Q(D_q), .clr(Reset));
  or or_3 (or_3_out, decoder_1_out2, demultiplexer_3_out2);
  Register H (.D(multiplexer_4_out), .en(or_4_out), .clk(Clock), .Q(H_q), .clr(Reset));
  or or_4 (or_4_out, decoder_1_out3, demultiplexer_3_out3);
  Register Z (.D(multiplexer_5_out), .en(or_5_out), .clk(Clock), .Q(Z_q), .clr(Reset));
  or or_5 (or_5_out, decoder_1_out4, demultiplexer_3_out0);
  Register C (.D(multiplexer_6_out), .en(or_6_out), .clk(Clock), .Q(C_q), .clr(Reset));
  or or_6 (or_6_out, decoder_1_out5, demultiplexer_3_out1);
  Register E (.D(multiplexer_7_out), .en(or_7_out), .clk(Clock), .Q(E_q), .clr(Reset));
  or or_7 (or_7_out, decoder_1_out6, demultiplexer_3_out2);
  Register L (.D(multiplexer_8_out), .en(or_8_out), .clk(Clock), .Q(L_q), .clr(Reset));
  or or_8 (or_8_out, decoder_1_out7, demultiplexer_3_out3);
  rozdzielac8to16 rozdzielac8to16_1 (.in_1(Z_q), .in_2(W_q), .out_3(rozdzielac8to16_1_out_3));
  rozdzielac8to16 rozdzielac8to16_2 (.in_1(C_q), .in_2(B_q), .out_3(rozdzielac8to16_2_out_3));
  rozdzielac8to16 rozdzielac8to16_3 (.in_1(E_q), .in_2(D_q), .out_3(rozdzielac8to16_3_out_3));
  rozdzielac8to16 rozdzielac8to16_4 (.in_1(L_q), .in_2(H_q), .out_3(rozdzielac8to16_4_out_3));
  Multiplexer #(.select(2), .width(16)) multiplexer_9 (
    .in0(rozdzielac8to16_1_out_3), .in1(rozdzielac8to16_2_out_3), .in2(rozdzielac8to16_3_out_3),
    .in3(rozdzielac8to16_4_out_3), .out(multiplexer_9_out), .sel(Address16));
  assign DataOut8 = xor_1_out ? multiplexer_10_out : 8'bz;  // Controlled_Buffer controlled_buffer_1
  Multiplexer #(.select(3), .width(8)) multiplexer_10 (
    .in0(W_q), .in1(B_q), .in2(D_q), .in3(H_q), .in4(Z_q), .in5(C_q), .in6(E_q), .in7(L_q),
    .out(multiplexer_10_out), .sel(Address8));
  xor xor_1 (xor_1_out, Pair, OutSwitch);
  Pull_Resistor pull_resistor_1 (.node(DataOut16));
  assign DataOut16 = and_1_out ? multiplexer_9_out : 16'bz;  // Controlled_Buffer controlled_buffer_2
  Pull_Resistor pull_resistor_2 (.node(DataOut8));
  and and_1 (and_1_out, OutSwitch, Pair);
endmodule

module rozdzielac8to16 (
  input  [7:0] in_1,
  input  [7:0] in_2,
  output [15:0] out_3
);


  assign out_3 = {in_2, in_1};
endmodule

module rozdzielacz16to8 (
  input  [15:0] in_1,
  output [7:0] out_2,
  output [7:0] out_3
);


  assign out_2 = in_1[7:0];
  assign out_3 = in_1[15:8];
endmodule

module akumulatorsum (
  input  [7:0] INDATA,
  input  in_2,
  input  CLK,
  output [7:0] OUTDATA,
  output FCER
);

  wire [7:0] adder_1_out;

  Register register_1 (.D(adder_1_out), .en(in_2), .clk(CLK), .Q(OUTDATA));  // open: clr
  Adder adder_1 (.a(OUTDATA), .b(INDATA), .out(adder_1_out), .cout(FCER));  // open: cin
endmodule

module Registers16 (
  input  [1:0] Address,
  input  [15:0] DataIn,
  input  Clock,
  input  Reset,
  input  OutSwitch,
  output [15:0] DataOut
);

  wire demultiplexer_2_out0, demultiplexer_2_out1, demultiplexer_2_out2;
  wire [15:0] demultiplexer_1_out0, demultiplexer_1_out1, demultiplexer_1_out2, IX_q, IY_q,
       multiplexer_1_out, SP_q;

  Demultiplexer #(.select(2), .width(16)) demultiplexer_1 (
    .out0(demultiplexer_1_out0), .out1(demultiplexer_1_out1), .out2(demultiplexer_1_out2), .in(DataIn),
    .sel(Address));  // open: out3
  Demultiplexer #(.select(2)) demultiplexer_2 (
    .out0(demultiplexer_2_out0), .out1(demultiplexer_2_out1), .out2(demultiplexer_2_out2), .sel(Address));  // open: out3, in
  Register #(.width(16)) IX (.D(demultiplexer_1_out0), .en(demultiplexer_2_out0), .clk(Clock), .Q(IX_q), .clr(Reset));
  Register #(.width(16)) IY (.D(demultiplexer_1_out1), .en(demultiplexer_2_out1), .clk(Clock), .Q(IY_q), .clr(Reset));
  Register #(.width(16)) SP (.D(demultiplexer_1_out2), .en(demultiplexer_2_out2), .clk(Clock), .Q(SP_q), .clr(Reset));
  assign DataOut = OutSwitch ? multiplexer_1_out : 16'bz;  // Controlled_Buffer controlled_buffer_1
  Multiplexer #(.select(2), .width(16)) multiplexer_1 (
    .in0(IX_q), .in1(IY_q), .in2(SP_q), .out(multiplexer_1_out));  // open: in3, sel
  Pull_Resistor pull_resistor_1 (.node(DataOut));
endmodule

module ALU (
  input  [7:0] DataIn1,
  input  [7:0] DataIn2,
  input  [7:0] FlagsIn,
  input  [4:0] InstAddr,
  input  SwitchOut,
  input  [2:0] BitAddr,
  output [7:0] FlagsOut,
  output [7:0] DataOut
);

  wire adder_1_cout, and_1_out, and_2_out, and_4_out, and_5_out, and_6_out, and_7_out, bitselector_1_out,
       decoder_1_out0, decoder_1_out1, decoder_1_out2, decoder_1_out3, decoder_1_out4, decoder_1_out5,
       decoder_1_out6, decoder_1_out7, decoder_1_out8, decoder_1_out9, decoder_1_out10, decoder_1_out11,
       decoder_1_out12, decoder_1_out13, decoder_1_out14, decoder_1_out15, decoder_1_out16, decoder_1_out17,
       inkrementacja_1_carry, nor_1_out, not_1_out, or_2_out, or_3_out, or_4_out, or_6_out, or_7_out,
       or_8_out, or_9_out, or_11_out, or_12_out, pull_resistor_6_node, subtractor_1_bout;
  wire [0:0] pull_resistor_7_node;
  wire [7:0] adder_1_out, and_3_out, controlled_buffer_5_out, controlled_buffer_6_out,
       controlled_buffer_7_out, controlled_buffer_8_out, controlled_buffer_9_out, controlled_buffer_10_out,
       controlled_buffer_11_out, controlled_buffer_12_out, controlled_buffer_13_out,
       controlled_buffer_14_out, controlled_buffer_15_out, controlled_buffer_16_out,
       controlled_buffer_17_out, controlled_buffer_18_out, controlled_buffer_19_out,
       controlled_buffer_20_out, controlled_buffer_21_out, controlled_buffer_22_out, dekrementacja_1_dataout,
       inkrementacja_1_dataout, multiplexer_1_out, or_10_out, or_13_out, pull_resistor_1_node,
       pull_resistor_2_node, pull_resistor_3_node, pull_resistor_4_node, resetbit_1_dataout,
       setbit_1_dataout, subtractor_1_out, xor_1_out;
  wire [7:7] pull_resistor_5_node;

  and and_1 (and_1_out, FlagsIn[3], not_1_out);
  Decoder #(.enable("false"), .select(5)) decoder_1 (
    .out0(decoder_1_out0), .out1(decoder_1_out1), .out2(decoder_1_out2), .out3(decoder_1_out3),
    .out4(decoder_1_out4), .out5(decoder_1_out5), .out6(decoder_1_out6), .out7(decoder_1_out7),
    .out8(decoder_1_out8), .out9(decoder_1_out9), .out10(decoder_1_out10), .out11(decoder_1_out11),
    .out12(decoder_1_out12), .out13(decoder_1_out13), .out14(decoder_1_out14), .out15(decoder_1_out15),
    .out16(decoder_1_out16), .out17(decoder_1_out17), .sel(InstAddr));  // open: out18, out19, out20, out21, out22, out23, out24, out25, out26, out27, out28, out29, out30, out31
  or or_1 (or_13_out[3], or_4_out, and_1_out);
  and and_2 (and_2_out, not_1_out, FlagsIn[1]);
  or or_2 (or_2_out, or_4_out, decoder_1_out14, or_6_out);
  not not_1 (not_1_out, or_6_out);
  or or_3 (or_3_out, decoder_1_out2, decoder_1_out3);
  or or_4 (or_4_out, decoder_1_out2, decoder_1_out1);
  or or_5 (or_13_out[1], or_4_out, and_2_out);
  or or_6 (or_6_out, decoder_1_out0, decoder_1_out2);
  or or_7 (or_7_out, decoder_1_out6, decoder_1_out5, decoder_1_out4);
  or or_8 (or_8_out, decoder_1_out2, decoder_1_out0);
  or or_9 (or_9_out, decoder_1_out1, decoder_1_out3);
  Pull_Resistor pull_resistor_1 (.node(pull_resistor_1_node));
  assign pull_resistor_1_node = or_8_out ? DataIn1 : 8'bz;  // Controlled_Buffer controlled_buffer_1
  Pull_Resistor pull_resistor_2 (.node(pull_resistor_2_node));
  assign pull_resistor_2_node = or_8_out ? DataIn2 : 8'bz;  // Controlled_Buffer controlled_buffer_2
  Pull_Resistor pull_resistor_3 (.node(pull_resistor_3_node));
  assign pull_resistor_3_node = or_9_out ? DataIn1 : 8'bz;  // Controlled_Buffer controlled_buffer_3
  Pull_Resistor pull_resistor_4 (.node(pull_resistor_4_node));
  assign pull_resistor_4_node = or_9_out ? DataIn2 : 8'bz;  // Controlled_Buffer controlled_buffer_4
  assign controlled_buffer_5_out = decoder_1_out4 ? DataIn1 : 8'bz;  // Controlled_Buffer controlled_buffer_5
  assign and_3_out = controlled_buffer_5_out & controlled_buffer_6_out;  // AND_Gate and_3, 8 bits wide
  assign controlled_buffer_6_out = decoder_1_out4 ? DataIn2 : 8'bz;  // Controlled_Buffer controlled_buffer_6
  assign controlled_buffer_7_out = decoder_1_out5 ? DataIn1 : 8'bz;  // Controlled_Buffer controlled_buffer_7
  assign or_10_out = controlled_buffer_7_out | controlled_buffer_8_out;  // OR_Gate or_10, 8 bits wide
  assign controlled_buffer_8_out = decoder_1_out5 ? DataIn2 : 8'bz;  // Controlled_Buffer controlled_buffer_8
  assign controlled_buffer_9_out = decoder_1_out6 ? DataIn1 : 8'bz;  // Controlled_Buffer controlled_buffer_9
  assign controlled_buffer_10_out = decoder_1_out6 ? DataIn2 : 8'bz;  // Controlled_Buffer controlled_buffer_10
  assign controlled_buffer_11_out = decoder_1_out7 ? DataIn1 : 8'bz;  // Controlled_Buffer controlled_buffer_11
  assign controlled_buffer_12_out = decoder_1_out7 ? DataIn2 : 8'bz;  // Controlled_Buffer controlled_buffer_12
  assign controlled_buffer_13_out = decoder_1_out8 ? DataIn1 : 8'bz;  // Controlled_Buffer controlled_buffer_13
  assign controlled_buffer_14_out = decoder_1_out9 ? DataIn1 : 8'bz;  // Controlled_Buffer controlled_buffer_14
  Pull_Resistor pull_resistor_5 (.node(pull_resistor_5_node[7]));
  assign controlled_buffer_15_out = decoder_1_out10 ? DataIn1 : 8'bz;  // Controlled_Buffer controlled_buffer_15
  assign controlled_buffer_16_out = decoder_1_out11 ? DataIn1 : 8'bz;  // Controlled_Buffer controlled_buffer_16
  assign controlled_buffer_17_out = decoder_1_out12 ? DataIn1 : 8'bz;  // Controlled_Buffer controlled_buffer_17
  assign controlled_buffer_18_out = decoder_1_out13 ? DataIn1 : 8'bz;  // Controlled_Buffer controlled_buffer_18
  assign controlled_buffer_19_out = decoder_1_out14 ? DataIn1 : 8'bz;  // Controlled_Buffer controlled_buffer_19
  assign controlled_buffer_20_out = decoder_1_out15 ? DataIn1 : 8'bz;  // Controlled_Buffer controlled_buffer_20
  assign controlled_buffer_21_out = decoder_1_out16 ? DataIn1 : 8'bz;  // Controlled_Buffer controlled_buffer_21
  assign controlled_buffer_22_out = decoder_1_out17 ? DataIn1 : 8'bz;  // Controlled_Buffer controlled_buffer_22
  BitSelector bitselector_1 (.in(controlled_buffer_22_out), .out(bitselector_1_out), .sel(BitAddr));
  and and_4 (and_4_out, FlagsIn[0], or_3_out);
  Adder adder_1 (
    .a(pull_resistor_1_node), .b(pull_resistor_2_node), .out(adder_1_out), .cin(and_4_out),
    .cout(adder_1_cout));
  or or_11 (or_11_out, adder_1_cout, inkrementacja_1_carry, subtractor_1_bout);
  Subtractor subtractor_1 (
    .a(pull_resistor_3_node), .b(pull_resistor_4_node), .out(subtractor_1_out), .bin(and_4_out),
    .bout(subtractor_1_bout));
  assign xor_1_out = controlled_buffer_9_out ^ controlled_buffer_10_out;  // XOR_Gate xor_1, 8 bits wide
  Pull_Resistor pull_resistor_6 (.node(pull_resistor_6_node));
  Comparator #(.mode("unsigned")) comparator_1 (
    .a(controlled_buffer_11_out), .b(controlled_buffer_12_out), .eq(pull_resistor_6_node));  // open: gt, lt
  Pull_Resistor pull_resistor_7 (.node(pull_resistor_7_node[0]));
  Pull_Resistor pull_resistor_8 (.node(bitselector_1_out));
  inkrementacja inkrementacja_1 (
    .DataIn(controlled_buffer_18_out), .DataOut(inkrementacja_1_dataout), .Carry(inkrementacja_1_carry));
  dekrementacja dekrementacja_1 (.DataIn(controlled_buffer_19_out), .DataOut(dekrementacja_1_dataout));
  setBit setbit_1 (.Address(BitAddr), .DataIn(controlled_buffer_20_out), .DataOut(setbit_1_dataout));
  resetBit resetbit_1 (.Address(BitAddr), .DataIn(controlled_buffer_21_out), .DataOut(resetbit_1_dataout));
  nor nor_1 (nor_1_out, or_7_out, or_2_out);
  and and_5 (and_5_out, or_2_out, or_11_out);
  or or_12 (or_12_out, pull_resistor_6_node, bitselector_1_out);
  and and_6 (and_6_out, nor_1_out, FlagsIn[0]);
  or or_13 (or_13_out[0], and_6_out, and_5_out);
  Multiplexer #(.select(5), .width(8)) multiplexer_1 (
    .in0(adder_1_out), .in1(subtractor_1_out), .in2(adder_1_out), .in3(subtractor_1_out), .in4(and_3_out),
    .in5(or_10_out), .in6(xor_1_out), .in8({controlled_buffer_13_out[6:0], pull_resistor_7_node[0]}),
    .in9({pull_resistor_5_node[7], controlled_buffer_14_out[7:1]}),
    .in10({{2{controlled_buffer_15_out[7]}}, controlled_buffer_15_out[6:1]}),
    .in11({controlled_buffer_16_out[6:0], controlled_buffer_16_out[7]}),
    .in12({controlled_buffer_17_out[0], controlled_buffer_17_out[7:1]}), .in13(inkrementacja_1_dataout),
    .in14(dekrementacja_1_dataout), .in15(setbit_1_dataout), .in16(resetbit_1_dataout),
    .out(multiplexer_1_out), .sel(InstAddr));  // open: in7, in17, in18, in19, in20, in21, in22, in23, in24, in25, in26, in27, in28, in29, in30, in31
  assign FlagsOut = SwitchOut ? or_13_out : 8'bz;  // Controlled_Buffer controlled_buffer_23
  assign DataOut = SwitchOut ? multiplexer_1_out : 8'bz;  // Controlled_Buffer controlled_buffer_24
  Pull_Resistor #(.pull(1)) pull_resistor_9 (.node(multiplexer_1_out[7]));
  Pull_Resistor #(.pull(1)) pull_resistor_10 (.node(multiplexer_1_out[6]));
  Pull_Resistor #(.pull(1)) pull_resistor_11 (.node(multiplexer_1_out[5]));
  Pull_Resistor #(.pull(1)) pull_resistor_12 (.node(multiplexer_1_out[4]));
  Pull_Resistor #(.pull(1)) pull_resistor_13 (.node(multiplexer_1_out[3]));
  Pull_Resistor #(.pull(1)) pull_resistor_14 (.node(multiplexer_1_out[2]));
  Pull_Resistor pull_resistor_15 (.node(FlagsOut));
  and and_7 (and_7_out, ~multiplexer_1_out[0], ~multiplexer_1_out[1], ~multiplexer_1_out[2], ~multiplexer_1_out[3], ~multiplexer_1_out[4], ~multiplexer_1_out[5], ~multiplexer_1_out[6], ~multiplexer_1_out[7]);  // AND_Gate
  Pull_Resistor #(.pull(1)) pull_resistor_16 (.node(multiplexer_1_out[1]));
  Pull_Resistor #(.pull(1)) pull_resistor_17 (.node(multiplexer_1_out[0]));
  Pull_Resistor pull_resistor_18 (.node(DataOut));
  or or_14 (or_13_out[6], and_7_out, or_12_out);
endmodule

module inkrementacja (
  input  [7:0] DataIn,
  output [7:0] DataOut,
  output Carry
);

  wire and_1_out, and_2_out, and_3_out, and_4_out, and_5_out, and_6_out, and_7_out;

  not not_1 (DataOut[0], DataIn[0]);
  and and_1 (and_1_out, 1'b1, DataIn[0]);
  xor xor_1 (DataOut[1], and_1_out, DataIn[1]);
  and and_2 (and_2_out, and_1_out, DataIn[1]);
  xor xor_2 (DataOut[2], and_2_out, DataIn[2]);
  and and_3 (and_3_out, and_2_out, DataIn[2]);
  xor xor_3 (DataOut[3], and_3_out, DataIn[3]);
  and and_4 (and_4_out, and_3_out, DataIn[3]);
  xor xor_4 (DataOut[4], and_4_out, DataIn[4]);
  and and_5 (and_5_out, and_4_out, DataIn[4]);
  xor xor_5 (DataOut[5], and_5_out, DataIn[5]);
  and and_6 (and_6_out, and_5_out, DataIn[5]);
  xor xor_6 (DataOut[6], and_6_out, DataIn[6]);
  and and_7 (and_7_out, and_6_out, DataIn[6]);
  xor xor_7 (DataOut[7], and_7_out, DataIn[7]);
  and and_8 (Carry, and_7_out, DataIn[7]);
endmodule

module dekrementacja (
  input  [7:0] DataIn,
  output [7:0] DataOut
);

  wire and_1_out, and_2_out, and_3_out, and_4_out, and_5_out, and_6_out, not_2_out, not_3_out, not_4_out,
       not_5_out, not_6_out, not_7_out;

  not not_1 (DataOut[0], DataIn[0]);
  not not_2 (not_2_out, DataIn[1]);
  not not_3 (not_3_out, DataIn[2]);
  not not_4 (not_4_out, DataIn[3]);
  not not_5 (not_5_out, DataIn[4]);
  not not_6 (not_6_out, DataIn[5]);
  not not_7 (not_7_out, DataIn[6]);
  xor xor_1 (DataOut[1], DataOut[0], DataIn[1]);
  and and_1 (and_1_out, DataOut[0], not_2_out);
  xor xor_2 (DataOut[2], and_1_out, DataIn[2]);
  and and_2 (and_2_out, and_1_out, not_3_out);
  xor xor_3 (DataOut[3], and_2_out, DataIn[3]);
  and and_3 (and_3_out, and_2_out, not_4_out);
  xor xor_4 (DataOut[4], and_3_out, DataIn[4]);
  and and_4 (and_4_out, and_3_out, not_5_out);
  xor xor_5 (DataOut[5], and_4_out, DataIn[5]);
  and and_5 (and_5_out, and_4_out, not_6_out);
  xor xor_6 (DataOut[6], and_5_out, DataIn[6]);
  and and_6 (and_6_out, and_5_out, not_7_out);
  xor xor_7 (DataOut[7], and_6_out, DataIn[7]);
endmodule

module setBit (
  input  [2:0] Address,
  input  [7:0] DataIn,
  output [7:0] DataOut
);

  wire decoder_1_out0, decoder_1_out1, decoder_1_out2, decoder_1_out3, decoder_1_out4, decoder_1_out5,
       decoder_1_out6, decoder_1_out7;

  Decoder #(.select(3)) decoder_1 (
    .out0(decoder_1_out0), .out1(decoder_1_out1), .out2(decoder_1_out2), .out3(decoder_1_out3),
    .out4(decoder_1_out4), .out5(decoder_1_out5), .out6(decoder_1_out6), .out7(decoder_1_out7),
    .sel(Address), .en(1'b1));
  or or_1 (DataOut[0], DataIn[0], decoder_1_out0);
  or or_2 (DataOut[1], DataIn[1], decoder_1_out1);
  or or_3 (DataOut[2], DataIn[2], decoder_1_out2);
  or or_4 (DataOut[3], DataIn[3], decoder_1_out3);
  or or_5 (DataOut[4], DataIn[4], decoder_1_out4);
  or or_6 (DataOut[5], DataIn[5], decoder_1_out5);
  or or_7 (DataOut[6], DataIn[6], decoder_1_out6);
  or or_8 (DataOut[7], DataIn[7], decoder_1_out7);
endmodule

module resetBit (
  input  [2:0] Address,
  input  [7:0] DataIn,
  output [7:0] DataOut
);

  wire decoder_1_out0, decoder_1_out1, decoder_1_out2, decoder_1_out3, decoder_1_out4, decoder_1_out5,
       decoder_1_out6, decoder_1_out7, not_1_out, not_2_out, not_3_out, not_4_out, not_5_out, not_6_out,
       not_7_out, not_8_out;

  Decoder #(.select(3)) decoder_1 (
    .out0(decoder_1_out0), .out1(decoder_1_out1), .out2(decoder_1_out2), .out3(decoder_1_out3),
    .out4(decoder_1_out4), .out5(decoder_1_out5), .out6(decoder_1_out6), .out7(decoder_1_out7), .sel(Address));  // open: en
  not not_1 (not_1_out, decoder_1_out0);
  not not_2 (not_2_out, decoder_1_out1);
  not not_3 (not_3_out, decoder_1_out2);
  not not_4 (not_4_out, decoder_1_out3);
  not not_5 (not_5_out, decoder_1_out4);
  not not_6 (not_6_out, decoder_1_out5);
  not not_7 (not_7_out, decoder_1_out6);
  not not_8 (not_8_out, decoder_1_out7);
  and and_1 (DataOut[0], DataIn[0], not_1_out);
  and and_2 (DataOut[1], DataIn[1], not_2_out);
  and and_3 (DataOut[2], DataIn[2], not_3_out);
  and and_4 (DataOut[3], DataIn[3], not_4_out);
  and and_5 (DataOut[4], DataIn[4], not_5_out);
  and and_6 (DataOut[5], DataIn[5], not_6_out);
  and and_7 (DataOut[6], DataIn[6], not_7_out);
  and and_8 (DataOut[7], DataIn[7], not_8_out);
endmodule
