// Logisim project v1.0.0.circ as structural Verilog
module main (
  input  in_1,
  input  [1:0] in_2,
  output [2:0] out_3,
  output [7:0] out_4,
  output [7:0] out_5
);

  wire adder_1_cout, clock_1_out, insdec_1_acuout, insdec_1_ex, insdec_1_exaf, pull_resistor_3_node;
  wire [0:0] insdec_1_acuin, insdec_1_aluflag;
  wire [1:0] demultiplexer_3_out0, demultiplexer_3_out1, insdec_1_regnr16;
  wire [2:0] demultiplexer_4_out0, demultiplexer_4_out1, demultiplexer_8_out0, demultiplexer_8_out1,
       demultiplexer_10_out0, demultiplexer_10_out1;
  wire [3:0] demultiplexer_5_out0, demultiplexer_5_out1, insdec_1_reg16on;
  wire [4:0] insdec_1_alucode;
  wire [7:0] A_q, alu_1_flagsout, Ap_q, controlled_buffer_1_out, demultiplexer_2_out0, demultiplexer_2_out1,
       demultiplexer_7_out0, demultiplexer_7_out1, demultiplexer_9_out0, demultiplexer_9_out1, F_q, Fp_q,
       inc8_1_dataout, Main_dataout8, Mainp_dataout8, multiplexer_3_out, multiplexer_4_out, rom_1_data;
  wire [15:0] demultiplexer_1_out0, demultiplexer_1_out1, demultiplexer_6_out1, incdecneu16_1_dataout,
       insdec_1_insadr, Main_dataout16, Mainp_dataout16, multiplexer_1_out, registers16_1_p2;

  ROM #(.addrWidth(16)) rom_1 (.addr(insdec_1_insadr), .data(rom_1_data));
  Clock clock_1 (.out(clock_1_out));
  InsDec insdec_1 (
    .DataIn(out_4), .InsCode(rom_1_data), .Clock(clock_1_out), .Flags(multiplexer_3_out),
    .AluFlag(insdec_1_aluflag[0]), .RegistersFlag(insdec_1_reg16on[3]), .DataOut(out_4),
    .AcuOut(insdec_1_acuout), .DataSet(insdec_1_reg16on[1]), .RegNr16(insdec_1_regnr16),
    .Reg16On(insdec_1_reg16on[0]), .AcuIn(insdec_1_acuin[0]), .RegNr8(out_3), .AluCode(insdec_1_alucode),
    .EXaf(insdec_1_exaf), .EX(insdec_1_ex), .InsAdr(insdec_1_insadr));
  Pull_Resistor pull_resistor_1 (.node(insdec_1_reg16on[1]));
  Demultiplexer #(.width(16)) demultiplexer_1 (
    .out0(demultiplexer_1_out0), .out1(demultiplexer_1_out1), .in(multiplexer_1_out), .sel(insdec_1_ex));
  Demultiplexer #(.width(8)) demultiplexer_2 (
    .out0(demultiplexer_2_out0), .out1(demultiplexer_2_out1), .in(out_4), .sel(insdec_1_ex));
  Demultiplexer #(.width(2)) demultiplexer_3 (
    .out0(demultiplexer_3_out0), .out1(demultiplexer_3_out1), .in(insdec_1_regnr16), .sel(insdec_1_ex));
  Demultiplexer #(.width(3)) demultiplexer_4 (
    .out0(demultiplexer_4_out0), .out1(demultiplexer_4_out1), .in(out_3), .sel(insdec_1_ex));
  Demultiplexer #(.width(4)) demultiplexer_5 (
    .out0(demultiplexer_5_out0), .out1(demultiplexer_5_out1),
    .in({insdec_1_reg16on[3], in_1, insdec_1_reg16on[1:0]}), .sel(insdec_1_ex));
  IncDecNeu16 incdecneu16_1 (.InsAddr(in_2), .DataIn(multiplexer_1_out), .DataOut(incdecneu16_1_dataout));
  Main_Registers Main (
    .DataIn16(demultiplexer_1_out0), .DataIn8(demultiplexer_2_out0), .Address16(demultiplexer_3_out0),
    .Address8(demultiplexer_4_out0), .Pair(demultiplexer_5_out0[0]), .Set(demultiplexer_5_out0[1]),
    .Reset(demultiplexer_5_out0[2]), .OutSwitch(demultiplexer_5_out0[3]), .DataOut16(Main_dataout16),
    .DataOut8(Main_dataout8));
  Main_Registers Mainp (
    .DataIn16(demultiplexer_1_out1), .DataIn8(demultiplexer_2_out1), .Address16(demultiplexer_3_out1),
    .Address8(demultiplexer_4_out1), .Pair(demultiplexer_5_out1[0]), .Set(demultiplexer_5_out1[1]),
    .Reset(demultiplexer_5_out1[2]), .OutSwitch(demultiplexer_5_out1[3]), .DataOut16(Mainp_dataout16),
    .DataOut8(Mainp_dataout8));
  // Registers16 registers16_1: pin names not known; wires that end beside it: incdecneu16_1_dataout, registers16_1_p2
  Multiplexer #(.width(16)) multiplexer_1 (
    .in0(Main_dataout16), .in1(Mainp_dataout16), .out(multiplexer_1_out), .sel(insdec_1_ex));
  Multiplexer #(.width(8)) multiplexer_2 (.in0(Main_dataout8), .in1(Mainp_dataout8), .out(out_4), .sel(insdec_1_ex));
  Demultiplexer #(.width(16)) demultiplexer_6 (
    .out0(multiplexer_1_out), .out1(demultiplexer_6_out1), .in(registers16_1_p2), .sel(pull_resistor_3_node));
  Pull_Resistor pull_resistor_2 (.node(demultiplexer_6_out1));
  Pull_Resistor pull_resistor_3 (.node(pull_resistor_3_node));
  Demultiplexer #(.width(8)) demultiplexer_7 (
    .out0(demultiplexer_7_out0), .out1(demultiplexer_7_out1), .in(alu_1_flagsout), .sel(insdec_1_exaf));
  Demultiplexer #(.width(3)) demultiplexer_8 (
    .out0(demultiplexer_8_out0), .out1(demultiplexer_8_out1), .in({in_1, 1'b0, insdec_1_aluflag[0]}),
    .sel(insdec_1_exaf));
  Demultiplexer #(.width(8)) demultiplexer_9 (
    .out0(demultiplexer_9_out0), .out1(demultiplexer_9_out1), .in(out_4), .sel(insdec_1_exaf));
  Demultiplexer #(.width(3)) demultiplexer_10 (
    .out0(demultiplexer_10_out0), .out1(demultiplexer_10_out1), .in({in_1, 1'b0, insdec_1_acuin[0]}),
    .sel(insdec_1_exaf));
  assign controlled_buffer_1_out = pull_resistor_3_node ? out_4 : 8'bz;  // Controlled_Buffer controlled_buffer_1
  Adder adder_1 (
    .a(controlled_buffer_1_out), .b(demultiplexer_6_out1[7:0]), .out(multiplexer_1_out[7:0]),
    .cout(adder_1_cout));  // open: cin
  Register #(.trigger("low")) F (
    .D(demultiplexer_7_out0), .en(demultiplexer_8_out0[0]), .clk(demultiplexer_8_out0[1]), .Q(F_q),
    .clr(demultiplexer_8_out0[2]));
  Register Fp (
    .D(demultiplexer_7_out1), .en(demultiplexer_8_out1[0]), .clk(demultiplexer_8_out1[1]), .Q(Fp_q),
    .clr(demultiplexer_8_out1[2]));
  Register #(.trigger("low")) A (
    .D(demultiplexer_9_out0), .en(demultiplexer_10_out0[0]), .clk(demultiplexer_10_out0[1]), .Q(A_q),
    .clr(demultiplexer_10_out0[2]));
  Register #(.trigger("low")) Ap (
    .D(demultiplexer_9_out1), .en(demultiplexer_10_out1[0]), .clk(demultiplexer_10_out1[1]), .Q(Ap_q),
    .clr(demultiplexer_10_out1[2]));
  Pull_Resistor pull_resistor_4 (.node(controlled_buffer_1_out));
  inc8 inc8_1 (.DataIn(demultiplexer_6_out1[15:8]), .DataOut(inc8_1_dataout));  // open: Carry
  Multiplexer #(.width(8)) multiplexer_3 (.in0(F_q), .in1(Fp_q), .out(multiplexer_3_out), .sel(insdec_1_exaf));
  assign out_4 = insdec_1_acuout ? multiplexer_4_out : 8'bz;  // Controlled_Buffer controlled_buffer_2
  Multiplexer #(.width(8)) multiplexer_4 (.in0(A_q), .in1(Ap_q), .out(multiplexer_4_out), .sel(insdec_1_exaf));
  Multiplexer #(.width(8)) multiplexer_5 (
    .in0(demultiplexer_6_out1[15:8]), .in1(inc8_1_dataout), .out(multiplexer_1_out[15:8]), .sel(adder_1_cout));
  assign out_4 = insdec_1_aluflag[0] ? out_5 : 8'bz;  // Controlled_Buffer controlled_buffer_3
  ALU alu_1 (
    .DataIn1(multiplexer_4_out), .DataIn2(out_4), .FlagsIn(multiplexer_3_out), .InstAddr(insdec_1_alucode),
    .SwitchOut(insdec_1_aluflag[0]), .FlagsOut(alu_1_flagsout), .DataOut(out_5));  // open: BitAddr
endmodule

module rejestr_przerzutnikowy (
  input  in_1,
  input  [7:0] in_2,
  output [7:0] out_3
);

  D_Flip_Flop d_ff_1 (.clk(in_1), .D(in_2[0]), .Q(out_3[0]));  // open: Qn, preset, reset
  D_Flip_Flop d_ff_2 (.clk(in_1), .D(in_2[1]), .Q(out_3[1]));  // open: Qn, preset, reset
  D_Flip_Flop d_ff_3 (.clk(in_1), .D(in_2[2]), .Q(out_3[2]));  // open: Qn, preset, reset
  D_Flip_Flop d_ff_4 (.clk(in_1), .D(in_2[3]), .Q(out_3[3]));  // open: Qn, preset, reset
  D_Flip_Flop d_ff_5 (.clk(in_1), .D(in_2[4]), .Q(out_3[4]));  // open: Qn, preset, reset
  D_Flip_Flop d_ff_6 (.clk(in_1), .D(in_2[5]), .Q(out_3[5]));  // open: Qn, preset, reset
  D_Flip_Flop d_ff_7 (.clk(in_1), .D(in_2[6]), .Q(out_3[6]));  // open: Qn, preset, reset
  D_Flip_Flop d_ff_8 (.clk(in_1), .D(in_2[7]), .Q(out_3[7]));  // open: Qn, preset, reset
endmodule

module Main_Registers (
  input  [15:0] DataIn16,
  input  [7:0] DataIn8,
  input  [1:0] Address16,
  input  [2:0] Address8,
  input  Pair,
  input  Set,
  input  Reset,
  input  OutSwitch,
  output [15:0] DataOut16,
  output [7:0] DataOut8
);

  wire and_1_out, decoder_1_out0, decoder_1_out1, decoder_1_out2, decoder_1_out3, decoder_1_out4,
       decoder_1_out5, decoder_1_out6, decoder_1_out7, demultiplexer_3_out0, demultiplexer_3_out1,
       demultiplexer_3_out2, demultiplexer_3_out3, not_1_out, or_1_out, or_2_out, or_3_out, or_4_out,
       or_5_out, or_6_out, or_7_out, or_8_out, xor_1_out;
  wire [7:0] B_q, C_q, D_q, demultiplexer_2_out0, demultiplexer_2_out1, demultiplexer_2_out2,
       demultiplexer_2_out3, demultiplexer_2_out4, demultiplexer_2_out5, demultiplexer_2_out6,
       demultiplexer_2_out7, E_q, H_q, L_q, multiplexer_1_out, multiplexer_2_out, multiplexer_3_out,
       multiplexer_4_out, multiplexer_5_out, multiplexer_6_out, multiplexer_7_out, multiplexer_8_out,
       multiplexer_10_out, rozdzielacz16to8_1_out_2, rozdzielacz16to8_1_out_3, rozdzielacz16to8_2_out_2,
       rozdzielacz16to8_2_out_3, rozdzielacz16to8_3_out_2, rozdzielacz16to8_3_out_3,
       rozdzielacz16to8_4_out_2, rozdzielacz16to8_4_out_3, W_q, Z_q;
  wire [15:0] demultiplexer_1_out0, demultiplexer_1_out1, demultiplexer_1_out2, demultiplexer_1_out3,
       multiplexer_9_out, rozdzielac8to16_1_out_3, rozdzielac8to16_2_out_3, rozdzielac8to16_3_out_3,
       rozdzielac8to16_4_out_3;

  rozdzielacz16to8 rozdzielacz16to8_1 (
    .in_1(demultiplexer_1_out0), .out_2(rozdzielacz16to8_1_out_2), .out_3(rozdzielacz16to8_1_out_3));
  rozdzielacz16to8 rozdzielacz16to8_2 (
    .in_1(demultiplexer_1_out1), .out_2(rozdzielacz16to8_2_out_2), .out_3(rozdzielacz16to8_2_out_3));
  Demultiplexer #(.select(2), .width(16)) demultiplexer_1 (
    .out0(demultiplexer_1_out0), .out1(demultiplexer_1_out1), .out2(demultiplexer_1_out2),
    .out3(demultiplexer_1_out3), .in(DataIn16), .sel(Address16));
  rozdzielacz16to8 rozdzielacz16to8_3 (
    .in_1(demultiplexer_1_out2), .out_2(rozdzielacz16to8_3_out_2), .out_3(rozdzielacz16to8_3_out_3));
  rozdzielacz16to8 rozdzielacz16to8_4 (
    .in_1(demultiplexer_1_out3), .out_2(rozdzielacz16to8_4_out_2), .out_3(rozdzielacz16to8_4_out_3));
  Demultiplexer #(.select(3), .width(8)) demultiplexer_2 (
    .out0(demultiplexer_2_out0), .out1(demultiplexer_2_out1), .out2(demultiplexer_2_out2),
    .out3(demultiplexer_2_out3), .out4(demultiplexer_2_out4), .out5(demultiplexer_2_out5),
    .out6(demultiplexer_2_out6), .out7(demultiplexer_2_out7), .in(DataIn8), .sel(Address8));
  Decoder #(.select(3)) decoder_1 (
    .out0(decoder_1_out0), .out1(decoder_1_out1), .out2(decoder_1_out2), .out3(decoder_1_out3),
    .out4(decoder_1_out4), .out5(decoder_1_out5), .out6(decoder_1_out6), .out7(decoder_1_out7),
    .sel(Address8), .en(not_1_out));
  not not_1 (not_1_out, Pair);
  Multiplexer #(.width(8)) multiplexer_1 (
    .in0(demultiplexer_2_out0), .in1(rozdzielacz16to8_1_out_2), .out(multiplexer_1_out), .sel(Pair));
  Multiplexer #(.width(8)) multiplexer_2 (
    .in0(demultiplexer_2_out1), .in1(rozdzielacz16to8_2_out_2), .out(multiplexer_2_out), .sel(Pair));
  Multiplexer #(.width(8)) multiplexer_3 (
    .in0(demultiplexer_2_out2), .in1(rozdzielacz16to8_3_out_2), .out(multiplexer_3_out), .sel(Pair));
  Multiplexer #(.width(8)) multiplexer_4 (
    .in0(demultiplexer_2_out3), .in1(rozdzielacz16to8_4_out_2), .out(multiplexer_4_out), .sel(Pair));
  Multiplexer #(.width(8)) multiplexer_5 (
    .in0(demultiplexer_2_out4), .in1(rozdzielacz16to8_1_out_3), .out(multiplexer_5_out), .sel(Pair));
  Multiplexer #(.width(8)) multiplexer_6 (
    .in0(demultiplexer_2_out5), .in1(rozdzielacz16to8_2_out_3), .out(multiplexer_6_out), .sel(Pair));
  Multiplexer #(.width(8)) multiplexer_7 (
    .in0(demultiplexer_2_out6), .in1(rozdzielacz16to8_3_out_3), .out(multiplexer_7_out), .sel(Pair));
  Multiplexer #(.width(8)) multiplexer_8 (
    .in0(demultiplexer_2_out7), .in1(rozdzielacz16to8_4_out_3), .out(multiplexer_8_out), .sel(Pair));
  Demultiplexer #(.select(2)) demultiplexer_3 (
    .out0(demultiplexer_3_out0), .out1(demultiplexer_3_out1), .out2(demultiplexer_3_out2),
    .out3(demultiplexer_3_out3), .in(Pair), .sel(Address16));
  Register #(.trigger("high")) B (.D(multiplexer_1_out), .en(or_1_out), .clk(Set), .Q(B_q), .clr(Reset));
  or or_1 (or_1_out, decoder_1_out0, demultiplexer_3_out0);
  Register #(.trigger("high")) C (.D(multiplexer_2_out), .en(or_2_out), .clk(Set), .Q(C_q), .clr(Reset));
  or or_2 (or_2_out, decoder_1_out1, demultiplexer_3_out0);
  Register #(.trigger("high")) D (.D(multiplexer_3_out), .en(or_3_out), .clk(Set), .Q(D_q), .clr(Reset));
  or or_3 (or_3_out, decoder_1_out2, demultiplexer_3_out1);
  Register #(.trigger("high")) E (.D(multiplexer_4_out), .en(or_4_out), .clk(Set), .Q(E_q), .clr(Reset));
  or or_4 (or_4_out, decoder_1_out3, demultiplexer_3_out1);
  Register #(.trigger("high")) H (.D(multiplexer_5_out), .en(or_5_out), .clk(Set), .Q(H_q), .clr(Reset));
  or or_5 (or_5_out, decoder_1_out4, demultiplexer_3_out2);
  Register #(.trigger("high")) L (.D(multiplexer_6_out), .en(or_6_out), .clk(Set), .Q(L_q), .clr(Reset));
  or or_6 (or_6_out, decoder_1_out5, demultiplexer_3_out2);
  Register #(.trigger("high")) W (.D(multiplexer_7_out), .en(or_7_out), .clk(Set), .Q(W_q), .clr(Reset));
  or or_7 (or_7_out, decoder_1_out6, demultiplexer_3_out3);
  Register #(.trigger("high")) Z (.D(multiplexer_8_out), .en(or_8_out), .clk(Set), .Q(Z_q), .clr(Reset));
  or or_8 (or_8_out, decoder_1_out7, demultiplexer_3_out3);
  rozdzielac8to16 rozdzielac8to16_1 (.in_1(H_q), .in_2(B_q), .out_3(rozdzielac8to16_1_out_3));
  rozdzielac8to16 rozdzielac8to16_2 (.in_1(L_q), .in_2(C_q), .out_3(rozdzielac8to16_2_out_3));
  rozdzielac8to16 rozdzielac8to16_3 (.in_1(W_q), .in_2(D_q), .out_3(rozdzielac8to16_3_out_3));
  rozdzielac8to16 rozdzielac8to16_4 (.in_1(Z_q), .in_2(E_q), .out_3(rozdzielac8to16_4_out_3));
  Multiplexer #(.select(2), .width(16)) multiplexer_9 (
    .in0(rozdzielac8to16_1_out_3), .in1(rozdzielac8to16_2_out_3), .in2(rozdzielac8to16_3_out_3),
    .in3(rozdzielac8to16_4_out_3), .out(multiplexer_9_out), .sel(Address16));
  assign DataOut8 = xor_1_out ? multiplexer_10_out : 8'bz;  // Controlled_Buffer controlled_buffer_1
  Multiplexer #(.select(3), .width(8)) multiplexer_10 (
    .in0(B_q), .in1(C_q), .in2(D_q), .in3(E_q), .in4(H_q), .in5(L_q), .in6(W_q), .in7(Z_q),
    .out(multiplexer_10_out), .sel(Address8));
  xor xor_1 (xor_1_out, Pair, OutSwitch);
  assign DataOut16 = and_1_out ? multiplexer_9_out : 16'bz;  // Controlled_Buffer controlled_buffer_2
  and and_1 (and_1_out, OutSwitch, Pair);
endmodule

module rozdzielac8to16 (
  input  [7:0] in_1,
  input  [7:0] in_2,
  output [15:0] out_3
);


  assign out_3 = {in_2, in_1};
endmodule

module rozdzielacz16to8 (
  input  [15:0] in_1,
  output [7:0] out_2,
  output [7:0] out_3
);


  assign out_2 = in_1[7:0];
  assign out_3 = in_1[15:8];
endmodule

module akumulatorsum (
  input  [7:0] INDATA,
  input  in_2,
  input  CLK,
  output [7:0] OUTDATA,
  output FCER
);

  wire [7:0] adder_1_out;

  Register register_1 (.D(adder_1_out), .en(in_2), .clk(CLK), .Q(OUTDATA));  // open: clr
  Adder adder_1 (.a(OUTDATA), .b(INDATA), .out(adder_1_out), .cout(FCER));  // open: cin
endmodule

module Registers16 (
  input  [1:0] Address,
  input  [15:0] DataIn,
  input  Clock,
  input  Reset,
  input  OutSwitch,
  output [15:0] DataOut
);

  wire demultiplexer_2_out0, demultiplexer_2_out1, demultiplexer_2_out2;
  wire [15:0] demultiplexer_1_out0, demultiplexer_1_out1, demultiplexer_1_out2, IX_q, IY_q,
       multiplexer_1_out, SP_q;

  Demultiplexer #(.select(2), .width(16)) demultiplexer_1 (
    .out0(demultiplexer_1_out0), .out1(demultiplexer_1_out1), .out2(demultiplexer_1_out2), .in(DataIn),
    .sel(Address));  // open: out3
  Demultiplexer #(.select(2)) demultiplexer_2 (
    .out0(demultiplexer_2_out0), .out1(demultiplexer_2_out1), .out2(demultiplexer_2_out2), .sel(Address));  // open: out3, in
  Register #(.width(16)) IX (.D(demultiplexer_1_out0), .en(demultiplexer_2_out0), .clk(Clock), .Q(IX_q), .clr(Reset));
  Register #(.width(16)) IY (.D(demultiplexer_1_out1), .en(demultiplexer_2_out1), .clk(Clock), .Q(IY_q), .clr(Reset));
  Register #(.width(16)) SP (.D(demultiplexer_1_out2), .en(demultiplexer_2_out2), .clk(Clock), .Q(SP_q), .clr(Reset));
  assign DataOut = OutSwitch ? multiplexer_1_out : 16'bz;  // Controlled_Buffer controlled_buffer_1
  Multiplexer #(.select(2), .width(16)) multiplexer_1 (
    .in0(IX_q), .in1(IY_q), .in2(SP_q), .out(multiplexer_1_out), .sel(Address));  // open: in3
  Pull_Resistor pull_resistor_1 (.node(DataOut));
endmodule

module ALU (
  input  [7:0] DataIn1,
  input  [7:0] DataIn2,
  input  [7:0] FlagsIn,
  input  [4:0] InstAddr,
  input  SwitchOut,
  input  [2:0] BitAddr,
  output [7:0] FlagsOut,
  output [7:0] DataOut
);

  wire adder_1_cout, and_1_out, and_2_out, and_3_out, and_4_out, and_6_out, and_7_out, and_8_out, and_9_out,
       and_10_out, bitselector_1_out, decoder_1_out0, decoder_1_out1, decoder_1_out2, decoder_1_out3,
       decoder_1_out4, decoder_1_out5, decoder_1_out6, decoder_1_out7, decoder_1_out8, decoder_1_out9,
       decoder_1_out10, decoder_1_out11, decoder_1_out12, decoder_1_out13, decoder_1_out14, decoder_1_out15,
       decoder_1_out16, decoder_1_out17, inc8_1_carry, nor_1_out, not_1_out, or_2_out, or_3_out, or_5_out,
       or_6_out, or_7_out, or_8_out, or_9_out, or_12_out, or_13_out, pull_resistor_6_node, subtractor_1_bout,
       xor_1_out;
  wire [0:0] pull_resistor_7_node;
  wire [6:0] or_14_out;
  wire [7:0] adder_1_out, and_5_out, controlled_buffer_5_out, controlled_buffer_6_out,
       controlled_buffer_7_out, controlled_buffer_8_out, controlled_buffer_9_out, controlled_buffer_10_out,
       controlled_buffer_11_out, controlled_buffer_12_out, controlled_buffer_13_out,
       controlled_buffer_14_out, controlled_buffer_15_out, controlled_buffer_16_out,
       controlled_buffer_17_out, controlled_buffer_18_out, controlled_buffer_19_out,
       controlled_buffer_20_out, controlled_buffer_21_out, controlled_buffer_22_out, dec8_1_dataout,
       inc8_1_dataout, multiplexer_1_out, or_10_out, pull_resistor_1_node, pull_resistor_2_node,
       pull_resistor_3_node, pull_resistor_4_node, resetbit_1_dataout, setbit_1_dataout, subtractor_1_out,
       xor_2_out;
  wire [7:7] pull_resistor_5_node;

  Decoder #(.enable("false"), .select(5)) decoder_1 (
    .out0(decoder_1_out0), .out1(decoder_1_out1), .out2(decoder_1_out2), .out3(decoder_1_out3),
    .out4(decoder_1_out4), .out5(decoder_1_out5), .out6(decoder_1_out6), .out7(decoder_1_out7),
    .out8(decoder_1_out8), .out9(decoder_1_out9), .out10(decoder_1_out10), .out11(decoder_1_out11),
    .out12(decoder_1_out12), .out13(decoder_1_out13), .out14(decoder_1_out14), .out15(decoder_1_out15),
    .out16(decoder_1_out16), .out17(decoder_1_out17), .sel(InstAddr));  // open: out18, out19, out20, out21, out22, out23, out24, out25, out26, out27, out28, out29, out30, out31
  or or_1 (or_14_out[3], or_3_out, and_1_out);
  and and_1 (and_1_out, FlagsIn[3], not_1_out);
  and and_2 (and_2_out, not_1_out, FlagsIn[1]);
  not not_1 (not_1_out, or_6_out);
  or or_2 (or_2_out, decoder_1_out2, decoder_1_out3);
  or or_3 (or_3_out, decoder_1_out2, decoder_1_out1);
  or or_4 (or_14_out[1], or_3_out, and_2_out);
  or or_5 (or_5_out, or_3_out, decoder_1_out14, or_6_out);
  or or_6 (or_6_out, decoder_1_out0, decoder_1_out2);
  or or_7 (or_7_out, decoder_1_out6, decoder_1_out5, decoder_1_out4);
  or or_8 (or_8_out, decoder_1_out2, decoder_1_out0);
  or or_9 (or_9_out, decoder_1_out1, decoder_1_out3);
  Pull_Resistor pull_resistor_1 (.node(pull_resistor_1_node));
  assign pull_resistor_1_node = or_8_out ? DataIn1 : 8'bz;  // Controlled_Buffer controlled_buffer_1
  Pull_Resistor pull_resistor_2 (.node(pull_resistor_2_node));
  assign pull_resistor_2_node = or_8_out ? DataIn2 : 8'bz;  // Controlled_Buffer controlled_buffer_2
  Pull_Resistor pull_resistor_3 (.node(pull_resistor_3_node));
  assign pull_resistor_3_node = or_9_out ? DataIn1 : 8'bz;  // Controlled_Buffer controlled_buffer_3
  Pull_Resistor pull_resistor_4 (.node(pull_resistor_4_node));
  assign pull_resistor_4_node = or_9_out ? DataIn2 : 8'bz;  // Controlled_Buffer controlled_buffer_4
  assign controlled_buffer_5_out = decoder_1_out4 ? DataIn1 : 8'bz;  // Controlled_Buffer controlled_buffer_5
  assign controlled_buffer_6_out = decoder_1_out4 ? DataIn2 : 8'bz;  // Controlled_Buffer controlled_buffer_6
  assign controlled_buffer_7_out = decoder_1_out5 ? DataIn1 : 8'bz;  // Controlled_Buffer controlled_buffer_7
  assign controlled_buffer_8_out = decoder_1_out5 ? DataIn2 : 8'bz;  // Controlled_Buffer controlled_buffer_8
  assign controlled_buffer_9_out = decoder_1_out6 ? DataIn1 : 8'bz;  // Controlled_Buffer controlled_buffer_9
  assign controlled_buffer_10_out = decoder_1_out6 ? DataIn2 : 8'bz;  // Controlled_Buffer controlled_buffer_10
  assign controlled_buffer_11_out = decoder_1_out7 ? DataIn1 : 8'bz;  // Controlled_Buffer controlled_buffer_11
  assign controlled_buffer_12_out = decoder_1_out7 ? DataIn2 : 8'bz;  // Controlled_Buffer controlled_buffer_12
  assign controlled_buffer_13_out = decoder_1_out8 ? DataIn1 : 8'bz;  // Controlled_Buffer controlled_buffer_13
  assign controlled_buffer_14_out = decoder_1_out9 ? DataIn1 : 8'bz;  // Controlled_Buffer controlled_buffer_14
  Pull_Resistor pull_resistor_5 (.node(pull_resistor_5_node[7]));
  assign controlled_buffer_15_out = decoder_1_out10 ? DataIn1 : 8'bz;  // Controlled_Buffer controlled_buffer_15
  assign controlled_buffer_16_out = decoder_1_out11 ? DataIn1 : 8'bz;  // Controlled_Buffer controlled_buffer_16
  assign controlled_buffer_17_out = decoder_1_out12 ? DataIn1 : 8'bz;  // Controlled_Buffer controlled_buffer_17
  assign controlled_buffer_18_out = decoder_1_out13 ? DataIn1 : 8'bz;  // Controlled_Buffer controlled_buffer_18
  assign controlled_buffer_19_out = decoder_1_out14 ? DataIn1 : 8'bz;  // Controlled_Buffer controlled_buffer_19
  assign controlled_buffer_20_out = decoder_1_out15 ? DataIn1 : 8'bz;  // Controlled_Buffer controlled_buffer_20
  assign controlled_buffer_21_out = decoder_1_out16 ? DataIn1 : 8'bz;  // Controlled_Buffer controlled_buffer_21
  assign controlled_buffer_22_out = decoder_1_out17 ? DataIn1 : 8'bz;  // Controlled_Buffer controlled_buffer_22
  BitSelector bitselector_1 (.in(controlled_buffer_22_out), .out(bitselector_1_out), .sel(BitAddr));
  xor xor_1 (xor_1_out, DataIn2[7], multiplexer_1_out[7]);
  and and_3 (and_3_out, DataIn2[7], DataIn1[7]);
  and and_4 (and_4_out, FlagsIn[0], or_2_out);
  Adder adder_1 (
    .a(pull_resistor_1_node), .b(pull_resistor_2_node), .out(adder_1_out), .cin(and_4_out),
    .cout(adder_1_cout));
  Subtractor subtractor_1 (
    .a(pull_resistor_3_node), .b(pull_resistor_4_node), .out(subtractor_1_out), .bin(and_4_out),
    .bout(subtractor_1_bout));
  assign and_5_out = controlled_buffer_5_out & controlled_buffer_6_out;  // AND_Gate and_5, 8 bits wide
  assign or_10_out = controlled_buffer_7_out | controlled_buffer_8_out;  // OR_Gate or_10, 8 bits wide
  assign xor_2_out = controlled_buffer_9_out ^ controlled_buffer_10_out;  // XOR_Gate xor_2, 8 bits wide
  Pull_Resistor pull_resistor_6 (.node(pull_resistor_6_node));
  Comparator #(.mode("unsigned")) comparator_1 (
    .a(controlled_buffer_11_out), .b(controlled_buffer_12_out), .eq(pull_resistor_6_node));  // open: gt, lt
  Pull_Resistor pull_resistor_7 (.node(pull_resistor_7_node[0]));
  inc8 inc8_1 (.DataIn(controlled_buffer_18_out), .DataOut(inc8_1_dataout), .Carry(inc8_1_carry));
  dec8 dec8_1 (.DataIn(controlled_buffer_19_out), .DataOut(dec8_1_dataout));
  setBit setbit_1 (.Address(BitAddr), .DataIn(controlled_buffer_20_out), .DataOut(setbit_1_dataout));
  resetBit resetbit_1 (.Address(BitAddr), .DataIn(controlled_buffer_21_out), .DataOut(resetbit_1_dataout));
  and and_6 (and_6_out, or_9_out, xor_1_out);
  or or_11 (or_14_out[5], and_6_out, and_7_out);
  and and_7 (and_7_out, xor_1_out, and_3_out, or_6_out);
  and and_8 (and_8_out, or_5_out, or_12_out);
  or or_12 (or_12_out, adder_1_cout, inc8_1_carry, subtractor_1_bout);
  or or_13 (or_13_out, pull_resistor_6_node, bitselector_1_out);
  Pull_Resistor pull_resistor_8 (.node(bitselector_1_out));
  nor nor_1 (nor_1_out, or_7_out, or_5_out);
  and and_9 (and_9_out, nor_1_out, FlagsIn[0]);
  or or_14 (or_14_out[0], and_9_out, and_8_out);
  Multiplexer #(.select(5), .width(8)) multiplexer_1 (
    .in0(adder_1_out), .in1(subtractor_1_out), .in2(adder_1_out), .in3(subtractor_1_out), .in4(and_5_out),
    .in5(or_10_out), .in6(xor_2_out), .in8({controlled_buffer_13_out[6:0], pull_resistor_7_node[0]}),
    .in9({pull_resistor_5_node[7], controlled_buffer_14_out[7:1]}),
    .in10({{2{controlled_buffer_15_out[7]}}, controlled_buffer_15_out[6:1]}),
    .in11({controlled_buffer_16_out[6:0], controlled_buffer_16_out[7]}),
    .in12({controlled_buffer_17_out[0], controlled_buffer_17_out[7:1]}), .in13(inc8_1_dataout),
    .in14(dec8_1_dataout), .in15(setbit_1_dataout), .in16(resetbit_1_dataout), .out(multiplexer_1_out),
    .sel(InstAddr));  // open: in7, in17, in18, in19, in20, in21, in22, in23, in24, in25, in26, in27, in28, in29, in30, in31
  Pull_Resistor #(.pull(1)) pull_resistor_9 (.node(multiplexer_1_out[7]));
  Pull_Resistor #(.pull(1)) pull_resistor_10 (.node(multiplexer_1_out[6]));
  Pull_Resistor #(.pull(1)) pull_resistor_11 (.node(multiplexer_1_out[5]));
  Pull_Resistor #(.pull(1)) pull_resistor_12 (.node(multiplexer_1_out[4]));
  Pull_Resistor pull_resistor_13 (.node(FlagsOut));
  assign FlagsOut = SwitchOut ? {multiplexer_1_out[7], or_14_out} : 8'bz;  // Controlled_Buffer controlled_buffer_23
  assign DataOut = SwitchOut ? multiplexer_1_out : 8'bz;  // Controlled_Buffer controlled_buffer_24
  Pull_Resistor #(.pull(1)) pull_resistor_14 (.node(multiplexer_1_out[3]));
  Pull_Resistor #(.pull(1)) pull_resistor_15 (.node(multiplexer_1_out[2]));
  Pull_Resistor #(.pull(1)) pull_resistor_16 (.node(multiplexer_1_out[1]));
  Pull_Resistor #(.pull(1)) pull_resistor_17 (.node(multiplexer_1_out[0]));
  Pull_Resistor pull_resistor_18 (.node(DataOut));
  and and_10 (and_10_out, ~multiplexer_1_out[0], ~multiplexer_1_out[1], ~multiplexer_1_out[2], ~multiplexer_1_out[3], ~multiplexer_1_out[4], ~multiplexer_1_out[5], ~multiplexer_1_out[6], ~multiplexer_1_out[7]);  // AND_Gate
  or or_15 (or_14_out[6], and_10_out, or_13_out);
endmodule

module inc8 (
  input  [7:0] DataIn,
  output [7:0] DataOut,
  output Carry
);

  wire and_1_out, and_2_out, and_3_out, and_4_out, and_5_out, and_6_out, and_7_out;

  not not_1 (DataOut[0], DataIn[0]);
  and and_1 (and_1_out, 1'b1, DataIn[0]);
  xor xor_1 (DataOut[1], and_1_out, DataIn[1]);
  and and_2 (and_2_out, and_1_out, DataIn[1]);
  xor xor_2 (DataOut[2], and_2_out, DataIn[2]);
  and and_3 (and_3_out, and_2_out, DataIn[2]);
  xor xor_3 (DataOut[3], and_3_out, DataIn[3]);
  and and_4 (and_4_out, and_3_out, DataIn[3]);
  xor xor_4 (DataOut[4], and_4_out, DataIn[4]);
  and and_5 (and_5_out, and_4_out, DataIn[4]);
  xor xor_5 (DataOut[5], and_5_out, DataIn[5]);
  and and_6 (and_6_out, and_5_out, DataIn[5]);
  xor xor_6 (DataOut[6], and_6_out, DataIn[6]);
  and and_7 (and_7_out, and_6_out, DataIn[6]);
  xor xor_7 (DataOut[7], and_7_out, DataIn[7]);
  and and_8 (Carry, and_7_out, DataIn[7]);
endmodule

module dec8 (
  input  [7:0] DataIn,
  output [7:0] DataOut
);

  wire and_1_out, and_2_out, and_3_out, and_4_out, and_5_out, and_6_out, not_2_out, not_3_out, not_4_out,
       not_5_out, not_6_out, not_7_out;

  not not_1 (DataOut[0], DataIn[0]);
  not not_2 (not_2_out, DataIn[1]);
  not not_3 (not_3_out, DataIn[2]);
  not not_4 (not_4_out, DataIn[3]);
  not not_5 (not_5_out, DataIn[4]);
  not not_6 (not_6_out, DataIn[5]);
  not not_7 (not_7_out, DataIn[6]);
  xor xor_1 (DataOut[1], DataOut[0], DataIn[1]);
  and and_1 (and_1_out, DataOut[0], not_2_out);
  xor xor_2 (DataOut[2], and_1_out, DataIn[2]);
  and and_2 (and_2_out, and_1_out, not_3_out);
  xor xor_3 (DataOut[3], and_2_out, DataIn[3]);
  and and_3 (and_3_out, and_2_out, not_4_out);
  xor xor_4 (DataOut[4], and_3_out, DataIn[4]);
  and and_4 (and_4_out, and_3_out, not_5_out);
  xor xor_5 (DataOut[5], and_4_out, DataIn[5]);
  and and_5 (and_5_out, and_4_out, not_6_out);
  xor xor_6 (DataOut[6], and_5_out, DataIn[6]);
  and and_6 (and_6_out, and_5_out, not_7_out);
  xor xor_7 (DataOut[7], and_6_out, DataIn[7]);
endmodule

module setBit (
  input  [2:0] Address,
  input  [7:0] DataIn,
  output [7:0] DataOut
);

  wire decoder_1_out0, decoder_1_out1, decoder_1_out2, decoder_1_out3, decoder_1_out4, decoder_1_out5,
       decoder_1_out6, decoder_1_out7;

  Decoder #(.select(3)) decoder_1 (
    .out0(decoder_1_out0), .out1(decoder_1_out1), .out2(decoder_1_out2), .out3(decoder_1_out3),
    .out4(decoder_1_out4), .out5(decoder_1_out5), .out6(decoder_1_out6), .out7(decoder_1_out7),
    .sel(Address), .en(1'b1));
  or or_1 (DataOut[0], DataIn[0], decoder_1_out0);
  or or_2 (DataOut[1], DataIn[1], decoder_1_out1);
  or or_3 (DataOut[2], DataIn[2], decoder_1_out2);
  or or_4 (DataOut[3], DataIn[3], decoder_1_out3);
  or or_5 (DataOut[4], DataIn[4], decoder_1_out4);
  or or_6 (DataOut[5], DataIn[5], decoder_1_out5);
  or or_7 (DataOut[6], DataIn[6], decoder_1_out6);
  or or_8 (DataOut[7], DataIn[7], decoder_1_out7);
endmodule

module resetBit (
  input  [2:0] Address,
  input  [7:0] DataIn,
  output [7:0] DataOut
);

  wire decoder_1_out0, decoder_1_out1, decoder_1_out2, decoder_1_out3, decoder_1_out4, decoder_1_out5,
       decoder_1_out6, decoder_1_out7, not_1_out, not_2_out, not_3_out, not_4_out, not_5_out, not_6_out,
       not_7_out, not_8_out;

  Decoder #(.select(3)) decoder_1 (
    .out0(decoder_1_out0), .out1(decoder_1_out1), .out2(decoder_1_out2), .out3(decoder_1_out3),
    .out4(decoder_1_out4), .out5(decoder_1_out5), .out6(decoder_1_out6), .out7(decoder_1_out7), .sel(Address));  // open: en
  not not_1 (not_1_out, decoder_1_out0);
  not not_2 (not_2_out, decoder_1_out1);
  not not_3 (not_3_out, decoder_1_out2);
  not not_4 (not_4_out, decoder_1_out3);
  not not_5 (not_5_out, decoder_1_out4);
  not not_6 (not_6_out, decoder_1_out5);
  not not_7 (not_7_out, decoder_1_out6);
  not not_8 (not_8_out, decoder_1_out7);
  and and_1 (DataOut[0], DataIn[0], not_1_out);
  and and_2 (DataOut[1], DataIn[1], not_2_out);
  and and_3 (DataOut[2], DataIn[2], not_3_out);
  and and_4 (DataOut[3], DataIn[3], not_4_out);
  and and_5 (DataOut[4], DataIn[4], not_5_out);
  and and_6 (DataOut[5], DataIn[5], not_6_out);
  and and_7 (DataOut[6], DataIn[6], not_7_out);
  and and_8 (DataOut[7], DataIn[7], not_8_out);
endmodule

module IncDecNeu16 (
  input  [1:0] InsAddr,
  input  [15:0] DataIn,
  output [15:0] DataOut
);

  wire [7:0] dec8_1_dataout, dec8_2_dataout, inc8_1_dataout, inc8_2_dataout;
  wire [15:0] demultiplexer_1_out0, demultiplexer_1_out1, demultiplexer_1_out2;

  Demultiplexer #(.select(2), .width(16)) demultiplexer_1 (
    .out0(demultiplexer_1_out0), .out1(demultiplexer_1_out1), .out2(demultiplexer_1_out2), .in(DataIn),
    .sel(InsAddr));  // open: out3
  inc8 inc8_1 (.DataIn(demultiplexer_1_out1[7:0]), .DataOut(inc8_1_dataout));  // open: Carry
  inc8 inc8_2 (.DataIn(demultiplexer_1_out1[15:8]), .DataOut(inc8_2_dataout));  // open: Carry
  dec8 dec8_1 (.DataIn(demultiplexer_1_out2[7:0]), .DataOut(dec8_1_dataout));
  dec8 dec8_2 (.DataIn(demultiplexer_1_out2[15:8]), .DataOut(dec8_2_dataout));
  Multiplexer #(.select(2), .width(16)) multiplexer_1 (
    .in0(demultiplexer_1_out0), .in1({inc8_2_dataout, inc8_1_dataout}),
    .in2({dec8_2_dataout, dec8_1_dataout}), .out(DataOut), .sel(InsAddr));  // open: in3
endmodule

module InsDec (
  input  [7:0] DataIn,
  input  [7:0] InsCode,
  input  Clock,
  input  [7:0] Flags,
  output AluFlag,
  output RegistersFlag,
  output [7:0] DataOut,
  output AcuOut,
  output DataSet,
  output [1:0] RegNr16,
  output Reg16On,
  output AcuIn,
  output [2:0] RegNr8,
  output [4:0] AluCode,
  output EXaf,
  output EX,
  output [15:0] InsAdr
);

  wire A_out, AdcR_out, adder_1_cout, AddR_out, and_1_out, and_2_out, and_3_out, and_4_out, and_5_out,
       and_6_out, and_7_out, and_8_out, and_9_out, and_10_out, and_11_out, and_12_out, and_13_out,
       and_14_out, and_15_out, and_16_out, and_17_out, and_18_out, and_19_out, and_20_out, and_21_out,
       and_22_out, and_23_out, and_24_out, and_25_out, and_26_out, and_27_out, and_28_out, and_29_out,
       and_30_out, and_31_out, and_32_out, and_33_out, and_34_out, and_35_out, and_36_out, and_37_out,
       and_38_out, and_39_out, and_40_out, and_41_out, and_42_out, and_43_out, and_44_out, AndR_out,
       controlled_buffer_4_out, controlled_buffer_11_out, controlled_buffer_13_out, CpR_out, d_ff_1_q,
       d_ff_2_q, d_ff_3_q, d_ff_4_q, d_ff_5_q, d_ff_6_q, d_ff_7_q, d_ff_7_qn, d_ff_8_q, d_ff_9_q, d_ff_10_q,
       d_ff_10_qn, d_ff_11_q, d_ff_12_q, d_ff_13_q, d_ff_14_q, d_ff_15_q, d_ff_16_q, d_ff_17_q, d_ff_18_q,
       DEC_out, Exafaf_out, EXX_out, inc8onoff_1_carry, INC_out, JPccnn_out, JPnn_out, JPx_out, LDrn_out,
       LDrr_out, nor_1_out, not_1_out, not_2_out, not_3_out, not_4_out, not_5_out, not_6_out, not_7_out,
       not_8_out, not_9_out, not_10_out, or_1_out, or_2_out, or_4_out, or_5_out, or_6_out, or_7_out,
       or_8_out, or_9_out, or_10_out, or_11_out, or_12_out, or_13_out, or_14_out, or_15_out, or_16_out,
       or_17_out, or_18_out, or_20_out, or_21_out, or_22_out, or_23_out, OrR_out, pull_resistor_2_node,
       pull_resistor_3_node, pull_resistor_10_node, SbcR_out, SubR_out, t_ff_1_q, t_ff_2_q, xor_1_out,
       xor_2_out, XorR_out;
  wire [2:0] controlled_buffer_5_out, multiplexer_4_out, multiplexer_5_out, register_7_q, xnor_3_out,
       xnor_6_out, xnor_7_out, xnor_8_out, xnor_9_out, xnor_11_out, xnor_12_out, xnor_13_out, xnor_14_out,
       xnor_16_out, xnor_17_out, xnor_18_out, xnor_21_out, xnor_22_out, xnor_23_out;
  wire [3:0] xnor_1_out, xnor_2_out, xnor_4_out, xnor_5_out, xnor_10_out, xnor_15_out, xnor_19_out,
       xnor_20_out;
  wire [7:0] adder_1_out, inc8onoff_1_dataout, multiplexer_3_out, register_1_q, register_3_q, register_4_q,
       register_6_q;
  wire [15:0] dec16_1_dataout, inc16_1_dataout, multiplexer_1_out, multiplexer_2_out, register_2_q,
       register_5_q;

  or or_1 (or_1_out, or_2_out, or_9_out);
  and and_1 (and_1_out, ~or_2_out, or_9_out);  // AND_Gate
  or or_2 (or_2_out, d_ff_3_q, d_ff_5_q, d_ff_1_q, d_ff_4_q, d_ff_2_q);
  D_Flip_Flop d_ff_1 (.clk(Clock), .D(and_1_out), .Q(d_ff_1_q));  // open: Qn, preset, reset
  Pull_Resistor pull_resistor_1 (.node(DataOut));
  or or_3 (DataSet, d_ff_17_q, t_ff_2_q);
  Pull_Resistor pull_resistor_2 (.node(pull_resistor_2_node));
  D_Flip_Flop d_ff_2 (.clk(Clock), .D(d_ff_1_q), .Q(d_ff_2_q));  // open: Qn, preset, reset
  assign DataOut = t_ff_2_q ? InsCode : 8'bz;  // Controlled_Buffer controlled_buffer_1
  xor xor_1 (xor_1_out, pull_resistor_2_node, t_ff_2_q);
  T_Flip_Flop t_ff_1 (.T(xor_1_out), .clk(Clock), .Q(t_ff_1_q));  // open: Qn, reset, preset
  D_Flip_Flop d_ff_3 (.clk(Clock), .D(d_ff_2_q), .Q(d_ff_3_q));  // open: Qn, preset, reset
  or or_4 (or_4_out, d_ff_1_q, or_5_out, d_ff_3_q);
  Register #(.width(16)) PC (.D(multiplexer_1_out), .en(1'b1), .clk(or_4_out), .Q(InsAdr));  // open: clr
  and LDrn (LDrn_out, ~InsCode[7], ~InsCode[6], InsCode[2], InsCode[1], ~InsCode[0]);  // AND_Gate
  not not_1 (not_1_out, or_13_out);
  assign pull_resistor_2_node = not_1_out ? LDrn_out : 1'bz;  // Controlled_Buffer controlled_buffer_2
  D_Flip_Flop d_ff_4 (.clk(Clock), .D(d_ff_3_q), .Q(d_ff_4_q));  // open: Qn, preset, reset
  D_Flip_Flop d_ff_5 (.clk(Clock), .D(d_ff_4_q), .Q(d_ff_5_q));  // open: Qn, preset, reset
  or or_5 (or_5_out, controlled_buffer_13_out, or_15_out, d_ff_5_q);
  Multiplexer #(.width(16)) multiplexer_1 (
    .in0(multiplexer_2_out), .in1({register_4_q, register_3_q}), .out(multiplexer_1_out), .sel(or_10_out));
  inc16 inc16_1 (.OnOff(1'b1), .DataIn(InsAdr), .DataOut(inc16_1_dataout));  // open: Carry
  dec16 dec16_1 (.DataIn(InsAdr), .DataOut(dec16_1_dataout));
  Pull_Resistor pull_resistor_3 (.node(pull_resistor_3_node));
  assign pull_resistor_3_node = not_2_out ? Clock : 1'bz;  // Controlled_Buffer controlled_buffer_3
  Register register_1 (.D(InsCode), .en(controlled_buffer_13_out), .clk(Clock), .Q(register_1_q), .clr(or_6_out));
  not not_2 (not_2_out, or_6_out);
  or or_6 (or_6_out, or_8_out, LDrr_out, or_7_out);
  assign controlled_buffer_4_out = xor_2_out ? Clock : 1'bz;  // Controlled_Buffer controlled_buffer_4
  Pull_Resistor pull_resistor_4 (.node(controlled_buffer_4_out));
  assign controlled_buffer_5_out = LDrn_out ? InsCode[5:3] : 3'bz;  // Controlled_Buffer controlled_buffer_5
  or or_7 (or_7_out, LDrn_out, or_13_out);
  T_Flip_Flop t_ff_2 (.T(t_ff_1_q), .clk(Clock), .Q(t_ff_2_q));  // open: Qn, reset, preset
  and and_2 (and_2_out, t_ff_1_q, ~t_ff_2_q);  // AND_Gate
  or or_8 (or_8_out, or_1_out, or_14_out, and_9_out);
  or or_9 (or_9_out, JPnn_out, and_5_out);
  or or_10 (or_10_out, d_ff_5_q, d_ff_4_q);
  Register #(.trigger("falling"), .width(16)) register_2 (
    .D(inc16_1_dataout), .en(1'b1), .clk(or_4_out), .Q(register_2_q));  // open: clr
  Multiplexer #(.width(16)) multiplexer_2 (
    .in0(register_2_q), .in1(register_5_q), .out(multiplexer_2_out), .sel(d_ff_9_q));
  or or_11 (or_11_out, or_12_out, and_3_out);
  or or_12 (or_12_out, d_ff_9_q, d_ff_11_q, d_ff_6_q);
  and and_3 (and_3_out, ~or_12_out, and_9_out);  // AND_Gate
  or or_13 (or_13_out, t_ff_2_q, d_ff_8_q, t_ff_1_q);
  xor xor_2 (xor_2_out, t_ff_2_q, t_ff_1_q);
  or or_14 (or_14_out, EXX_out, Exafaf_out);
  and JPnn (JPnn_out, InsCode[7], InsCode[6], ~InsCode[5], ~InsCode[4], ~InsCode[3], ~InsCode[2], InsCode[1], InsCode[0]);  // AND_Gate
  or or_15 (or_15_out, or_16_out, or_11_out, d_ff_11_q);
  D_Flip_Flop d_ff_6 (.clk(Clock), .D(and_3_out), .Q(d_ff_6_q));  // open: Qn, preset, reset
  Adder adder_1 (.a(InsCode), .b(dec16_1_dataout[7:0]), .out(adder_1_out), .cout(adder_1_cout));  // open: cin
  inc8OnOff inc8onoff_1 (
    .OnOff(adder_1_cout), .DataIn(dec16_1_dataout[15:8]), .DataOut(inc8onoff_1_dataout),
    .Carry(inc8onoff_1_carry));
  D_Flip_Flop d_ff_7 (.clk(pull_resistor_3_node), .D(d_ff_7_qn), .Q(d_ff_7_q), .Qn(d_ff_7_qn));  // open: preset, reset
  assign xnor_1_out = ~({register_1_q[7], register_1_q[5:3]} ^ 4'b1000);  // XNOR_Gate xnor_1, 4 bits wide
  not not_3 (not_3_out, register_1_q[6]);
  and AddR (AddR_out, xnor_1_out[3], xnor_1_out[2], xnor_1_out[1], xnor_1_out[0]);
  and and_4 (and_4_out, not_3_out, AddR_out);
  assign controlled_buffer_5_out = and_4_out ? register_1_q[2:0] : 3'bz;  // Controlled_Buffer controlled_buffer_6
  assign AluCode = AddR_out ? {5{1'b0}} : 5'bz;  // Controlled_Buffer controlled_buffer_7
  D_Flip_Flop d_ff_8 (.clk(Clock), .D(t_ff_2_q), .Q(d_ff_8_q));  // open: Qn, preset, reset
  and JPccnn (JPccnn_out, InsCode[7], InsCode[6], ~InsCode[2], InsCode[1], ~InsCode[0]);  // AND_Gate
  and and_5 (and_5_out, JPccnn_out, or_17_out);
  Register #(.trigger("high")) register_3 (.D(InsCode), .en(1'b1), .clk(d_ff_2_q), .Q(register_3_q));  // open: clr
  Register #(.trigger("high")) register_4 (.D(InsCode), .en(1'b1), .clk(d_ff_4_q), .Q(register_4_q));  // open: clr
  D_Flip_Flop d_ff_9 (.clk(Clock), .D(d_ff_6_q), .Q(d_ff_9_q));  // open: Qn, preset, reset
  Register #(.width(16)) register_5 (
    .D({multiplexer_3_out, adder_1_out}), .en(1'b1), .clk(d_ff_6_q), .Q(register_5_q));  // open: clr
  Multiplexer #(.width(8)) multiplexer_3 (
    .in0(inc8onoff_1_dataout), .in1({8{1'b0}}), .out(multiplexer_3_out), .sel(inc8onoff_1_carry));
  D_Flip_Flop d_ff_10 (.clk(d_ff_7_q), .D(d_ff_10_qn), .Q(d_ff_10_q), .Qn(d_ff_10_qn));  // open: preset, reset
  assign xnor_2_out = ~({register_1_q[7], register_1_q[5:3]} ^ 4'b1001);  // XNOR_Gate xnor_2, 4 bits wide
  and AdcR (AdcR_out, xnor_2_out[3], xnor_2_out[2], xnor_2_out[1], xnor_2_out[0]);
  and and_6 (and_6_out, not_3_out, AdcR_out);
  assign controlled_buffer_5_out = and_6_out ? register_1_q[2:0] : 3'bz;  // Controlled_Buffer controlled_buffer_8
  assign AluCode = AdcR_out ? 5'b00010 : 5'bz;  // Controlled_Buffer controlled_buffer_9
  assign AluCode = SubR_out ? 5'b00001 : 5'bz;  // Controlled_Buffer controlled_buffer_10
  or or_16 (or_16_out, d_ff_8_q, d_ff_14_q, d_ff_17_q, and_2_out, d_ff_18_q);
  assign xnor_3_out = ~(InsCode[5:3] ^ 3'b000);  // XNOR_Gate xnor_3, 3 bits wide
  and and_7 (and_7_out, xnor_3_out[2], xnor_3_out[1], xnor_3_out[0]);
  not not_4 (not_4_out, Flags[6]);
  and and_8 (and_8_out, and_7_out, not_4_out);
  and JPx (JPx_out, ~InsCode[7], ~InsCode[6], ~InsCode[2], ~InsCode[1], ~InsCode[0]);  // AND_Gate
  D_Flip_Flop d_ff_11 (.clk(Clock), .D(d_ff_9_q), .Q(d_ff_11_q));  // open: Qn, preset, reset
  and and_9 (and_9_out, JPx_out, or_18_out);
  and and_10 (and_10_out, ~d_ff_7_q, d_ff_10_q);  // AND_Gate
  assign controlled_buffer_11_out = not_2_out ? and_10_out : 1'bz;  // Controlled_Buffer controlled_buffer_11
  and and_11 (and_11_out, d_ff_7_q, ~d_ff_10_q);  // AND_Gate
  assign AluFlag = not_2_out ? and_11_out : 1'bz;  // Controlled_Buffer controlled_buffer_12
  and and_12 (and_12_out, ~d_ff_7_q, ~d_ff_10_q);  // AND_Gate
  assign controlled_buffer_13_out = not_2_out ? and_12_out : 1'bz;  // Controlled_Buffer controlled_buffer_13
  assign xnor_4_out = ~({register_1_q[7], register_1_q[5:3]} ^ 4'b1010);  // XNOR_Gate xnor_4, 4 bits wide
  assign xnor_5_out = ~({register_1_q[7], register_1_q[5:3]} ^ 4'b1011);  // XNOR_Gate xnor_5, 4 bits wide
  and SubR (SubR_out, xnor_4_out[3], xnor_4_out[2], xnor_4_out[1], xnor_4_out[0]);
  and SbcR (SbcR_out, xnor_5_out[3], xnor_5_out[2], xnor_5_out[1], xnor_5_out[0]);
  and and_13 (and_13_out, not_3_out, SubR_out);
  and and_14 (and_14_out, not_3_out, SbcR_out);
  assign controlled_buffer_5_out = and_13_out ? register_1_q[2:0] : 3'bz;  // Controlled_Buffer controlled_buffer_14
  assign controlled_buffer_5_out = and_14_out ? register_1_q[2:0] : 3'bz;  // Controlled_Buffer controlled_buffer_15
  assign AluCode = SbcR_out ? 5'b00011 : 5'bz;  // Controlled_Buffer controlled_buffer_16
  T_Flip_Flop #(.trigger("falling")) t_ff_3 (.T(EXX_out), .clk(Clock), .Q(EX));  // open: Qn, reset, preset
  and EXX (EXX_out, InsCode[0], ~InsCode[1], ~InsCode[2], InsCode[3], InsCode[4], ~InsCode[5], InsCode[6], InsCode[7]);  // AND_Gate
  assign xnor_6_out = ~(InsCode[5:3] ^ 3'b001);  // XNOR_Gate xnor_6, 3 bits wide
  assign xnor_7_out = ~(InsCode[5:3] ^ 3'b010);  // XNOR_Gate xnor_7, 3 bits wide
  and and_15 (and_15_out, xnor_6_out[2], xnor_6_out[1], xnor_6_out[0]);
  and and_16 (and_16_out, xnor_7_out[2], xnor_7_out[1], xnor_7_out[0]);
  not not_5 (not_5_out, Flags[0]);
  and and_17 (and_17_out, and_15_out, Flags[6]);
  and and_18 (and_18_out, and_16_out, not_5_out);
  assign xnor_8_out = ~(InsCode[5:3] ^ 3'b111);  // XNOR_Gate xnor_8, 3 bits wide
  assign xnor_9_out = ~(InsCode[5:3] ^ 3'b110);  // XNOR_Gate xnor_9, 3 bits wide
  and and_19 (and_19_out, xnor_8_out[2], xnor_8_out[1], xnor_8_out[0]);
  and and_20 (and_20_out, xnor_9_out[2], xnor_9_out[1], xnor_9_out[0]);
  not not_6 (not_6_out, Flags[0]);
  and and_21 (and_21_out, and_19_out, not_6_out);
  and and_22 (and_22_out, and_20_out, Flags[0]);
  Pull_Resistor pull_resistor_5 (.node(controlled_buffer_11_out));
  Pull_Resistor pull_resistor_6 (.node(AluFlag));
  Pull_Resistor pull_resistor_7 (.node(controlled_buffer_13_out));
  assign xnor_10_out = ~({register_1_q[7], register_1_q[5:3]} ^ 4'b1100);  // XNOR_Gate xnor_10, 4 bits wide
  and AndR (AndR_out, xnor_10_out[3], xnor_10_out[2], xnor_10_out[1], xnor_10_out[0]);
  and and_23 (and_23_out, not_3_out, AndR_out);
  assign controlled_buffer_5_out = and_23_out ? register_1_q[2:0] : 3'bz;  // Controlled_Buffer controlled_buffer_17
  assign AluCode = AndR_out ? 5'b00100 : 5'bz;  // Controlled_Buffer controlled_buffer_18
  assign xnor_11_out = ~(InsCode[5:3] ^ 3'b011);  // XNOR_Gate xnor_11, 3 bits wide
  assign xnor_12_out = ~(InsCode[5:3] ^ 3'b100);  // XNOR_Gate xnor_12, 3 bits wide
  and and_24 (and_24_out, xnor_11_out[2], xnor_11_out[1], xnor_11_out[0]);
  and and_25 (and_25_out, xnor_12_out[2], xnor_12_out[1], xnor_12_out[0]);
  not not_7 (not_7_out, Flags[5]);
  and and_26 (and_26_out, and_24_out, Flags[0]);
  and and_27 (and_27_out, and_25_out, not_7_out);
  or or_17 (or_17_out, and_8_out, and_17_out, and_18_out, and_26_out, and_27_out, and_35_out, and_36_out, and_41_out);
  assign xnor_13_out = ~(InsCode[5:3] ^ 3'b101);  // XNOR_Gate xnor_13, 3 bits wide
  assign xnor_14_out = ~(InsCode[5:3] ^ 3'b100);  // XNOR_Gate xnor_14, 3 bits wide
  and and_28 (and_28_out, xnor_13_out[2], xnor_13_out[1], xnor_13_out[0]);
  and and_29 (and_29_out, xnor_14_out[2], xnor_14_out[1], xnor_14_out[0]);
  not not_8 (not_8_out, Flags[6]);
  and and_30 (and_30_out, and_28_out, not_8_out);
  and and_31 (and_31_out, and_29_out, Flags[6]);
  or or_18 (or_18_out, and_21_out, and_22_out, and_37_out, and_30_out, and_31_out);
  Register #(.trigger("falling")) register_6 (.D(DataIn), .en(d_ff_13_q), .clk(Clock), .Q(register_6_q));  // open: clr
  assign DataOut = d_ff_17_q ? register_6_q : 8'bz;  // Controlled_Buffer controlled_buffer_19
  assign xnor_15_out = ~({register_1_q[7], register_1_q[5:3]} ^ 4'b1110);  // XNOR_Gate xnor_15, 4 bits wide
  and OrR (OrR_out, xnor_15_out[3], xnor_15_out[2], xnor_15_out[1], xnor_15_out[0]);
  and and_32 (and_32_out, not_3_out, OrR_out);
  assign controlled_buffer_5_out = and_32_out ? register_1_q[2:0] : 3'bz;  // Controlled_Buffer controlled_buffer_20
  assign AluCode = OrR_out ? 5'b00101 : 5'bz;  // Controlled_Buffer controlled_buffer_21
  assign AluCode = XorR_out ? 5'b00110 : 5'bz;  // Controlled_Buffer controlled_buffer_22
  and Exafaf (Exafaf_out, ~InsCode[0], ~InsCode[1], ~InsCode[2], InsCode[3], ~InsCode[4], ~InsCode[5], ~InsCode[6], ~InsCode[7]);  // AND_Gate
  assign xnor_16_out = ~(InsCode[5:3] ^ 3'b101);  // XNOR_Gate xnor_16, 3 bits wide
  assign xnor_17_out = ~(InsCode[5:3] ^ 3'b110);  // XNOR_Gate xnor_17, 3 bits wide
  and and_33 (and_33_out, xnor_16_out[2], xnor_16_out[1], xnor_16_out[0]);
  and and_34 (and_34_out, xnor_17_out[2], xnor_17_out[1], xnor_17_out[0]);
  not not_9 (not_9_out, Flags[7]);
  and and_35 (and_35_out, and_33_out, Flags[5]);
  and and_36 (and_36_out, and_34_out, not_9_out);
  assign xnor_18_out = ~(InsCode[5:3] ^ 3'b011);  // XNOR_Gate xnor_18, 3 bits wide
  and and_37 (and_37_out, xnor_18_out[2], xnor_18_out[1], xnor_18_out[0]);
  assign xnor_19_out = ~({register_1_q[7], register_1_q[5:3]} ^ 4'b1101);  // XNOR_Gate xnor_19, 4 bits wide
  assign xnor_20_out = ~({register_1_q[7], register_1_q[5:3]} ^ 4'b1111);  // XNOR_Gate xnor_20, 4 bits wide
  and XorR (XorR_out, xnor_19_out[3], xnor_19_out[2], xnor_19_out[1], xnor_19_out[0]);
  and CpR (CpR_out, xnor_20_out[3], xnor_20_out[2], xnor_20_out[1], xnor_20_out[0]);
  and and_38 (and_38_out, not_3_out, XorR_out);
  and and_39 (and_39_out, not_3_out, CpR_out);
  assign controlled_buffer_5_out = and_38_out ? register_1_q[2:0] : 3'bz;  // Controlled_Buffer controlled_buffer_23
  assign controlled_buffer_5_out = and_39_out ? register_1_q[2:0] : 3'bz;  // Controlled_Buffer controlled_buffer_24
  assign AluCode = CpR_out ? 5'b00111 : 5'bz;  // Controlled_Buffer controlled_buffer_25
  T_Flip_Flop #(.trigger("falling")) t_ff_4 (.T(Exafaf_out), .clk(Clock), .Q(EXaf));  // open: Qn, reset, preset
  assign xnor_21_out = ~(InsCode[5:3] ^ 3'b111);  // XNOR_Gate xnor_21, 3 bits wide
  and and_40 (and_40_out, xnor_21_out[2], xnor_21_out[1], xnor_21_out[0]);
  and and_41 (and_41_out, and_40_out, Flags[7]);
  or or_19 (RegistersFlag, controlled_buffer_11_out, d_ff_13_q);
  assign controlled_buffer_5_out = INC_out ? InsCode[5:3] : 3'bz;  // Controlled_Buffer controlled_buffer_26
  assign controlled_buffer_5_out = DEC_out ? InsCode[5:3] : 3'bz;  // Controlled_Buffer controlled_buffer_27
  or or_20 (or_20_out, d_ff_14_q, d_ff_12_q);
  and and_42 (and_42_out, ~or_20_out, EXX_out);  // AND_Gate
  and LDrr (LDrr_out, InsCode[6], ~InsCode[7]);  // AND_Gate
  and and_43 (and_43_out, ~or_21_out, LDrr_out);  // AND_Gate
  Multiplexer #(.width(3)) multiplexer_4 (
    .in0(InsCode[5:3]), .in1(InsCode[2:0]), .out(multiplexer_4_out), .sel(or_23_out));
  and INC (INC_out, ~InsCode[7], ~InsCode[6], InsCode[2], ~InsCode[1], ~InsCode[0]);  // AND_Gate
  assign AluCode = INC_out ? 5'b01011 : 5'bz;  // Controlled_Buffer controlled_buffer_28
  and DEC (DEC_out, ~InsCode[7], ~InsCode[6], InsCode[2], ~InsCode[1], InsCode[0]);  // AND_Gate
  assign AluCode = DEC_out ? 5'b01100 : 5'bz;  // Controlled_Buffer controlled_buffer_29
  D_Flip_Flop d_ff_12 (.clk(Clock), .D(and_42_out), .Q(d_ff_12_q));  // open: Qn, preset, reset
  or or_21 (or_21_out, d_ff_17_q, d_ff_15_q, d_ff_13_q);
  D_Flip_Flop d_ff_13 (.clk(Clock), .D(and_43_out), .Q(d_ff_13_q));  // open: Qn, preset, reset
  assign controlled_buffer_5_out = LDrr_out ? multiplexer_4_out : 3'bz;  // Controlled_Buffer controlled_buffer_30
  Pull_Resistor pull_resistor_8 (.node(controlled_buffer_5_out));
  Register #(.width(3)) register_7 (
    .D(controlled_buffer_5_out), .en(pull_resistor_2_node), .clk(controlled_buffer_4_out), .Q(register_7_q));  // open: clr
  or or_22 (or_22_out, d_ff_18_q, d_ff_16_q);
  D_Flip_Flop d_ff_14 (.clk(Clock), .D(d_ff_12_q), .Q(d_ff_14_q));  // open: Qn, preset, reset
  D_Flip_Flop d_ff_15 (.clk(Clock), .D(d_ff_13_q), .Q(d_ff_15_q));  // open: Qn, preset, reset
  or or_23 (or_23_out, d_ff_15_q, d_ff_17_q);
  assign xnor_22_out = ~(3'b110 ^ multiplexer_5_out);  // XNOR_Gate xnor_22, 3 bits wide
  assign xnor_23_out = ~(3'b111 ^ multiplexer_5_out);  // XNOR_Gate xnor_23, 3 bits wide
  D_Flip_Flop d_ff_16 (.clk(Clock), .D(and_44_out), .Q(d_ff_16_q));  // open: Qn, preset, reset
  and and_44 (and_44_out, ~or_22_out, Exafaf_out);  // AND_Gate
  D_Flip_Flop d_ff_17 (.clk(Clock), .D(d_ff_15_q), .Q(d_ff_17_q));  // open: Qn, preset, reset
  and HL (Reg16On, xnor_22_out[0], xnor_22_out[1], xnor_22_out[2]);
  and A (A_out, xnor_23_out[0], xnor_23_out[1], xnor_23_out[2]);
  nor nor_1 (nor_1_out, A_out, Reg16On);
  Pull_Resistor pull_resistor_9 (.node(RegNr8));
  assign RegNr8 = nor_1_out ? multiplexer_5_out : 3'bz;  // Controlled_Buffer controlled_buffer_31
  Multiplexer #(.width(3)) multiplexer_5 (
    .in0(controlled_buffer_5_out), .in1(register_7_q), .out(multiplexer_5_out), .sel(or_13_out));
  D_Flip_Flop d_ff_18 (.clk(Clock), .D(d_ff_16_q), .Q(d_ff_18_q));  // open: Qn, preset, reset
  and and_45 (AcuOut, d_ff_13_q, pull_resistor_10_node);
  assign RegNr16 = Reg16On ? 2'b10 : 2'bz;  // Controlled_Buffer controlled_buffer_32
  not not_10 (not_10_out, d_ff_13_q);
  Pull_Resistor pull_resistor_10 (.node(pull_resistor_10_node));
  assign pull_resistor_10_node = not_10_out ? A_out : 1'bz;  // Controlled_Buffer controlled_buffer_33
  Pull_Resistor pull_resistor_11 (.node(AluCode));
  and and_46 (AcuIn, pull_resistor_10_node, DataSet);
  Pull_Resistor pull_resistor_12 (.node(RegNr16));
  Pull_Resistor pull_resistor_13 (.node(Reg16On));
endmodule

module inc16 (
  input  OnOff,
  input  [15:0] DataIn,
  output [15:0] DataOut,
  output Carry
);

  wire and_1_out, and_2_out, and_3_out, and_4_out, and_5_out, and_6_out, and_7_out, and_8_out, and_9_out,
       and_10_out, and_11_out, and_12_out, and_13_out, and_14_out, and_15_out, not_1_out;

  not not_1 (not_1_out, OnOff);
  assign DataOut[0] = not_1_out ? DataIn[0] : 1'bz;  // Controlled_Buffer controlled_buffer_1
  assign DataOut[0] = OnOff ? ~DataIn[0] : 1'bz;  // Controlled_Inverter controlled_inverter_1
  and and_1 (and_1_out, OnOff, DataIn[0]);
  xor xor_1 (DataOut[1], and_1_out, DataIn[1]);
  and and_2 (and_2_out, and_1_out, DataIn[1]);
  xor xor_2 (DataOut[2], and_2_out, DataIn[2]);
  and and_3 (and_3_out, and_2_out, DataIn[2]);
  xor xor_3 (DataOut[3], and_3_out, DataIn[3]);
  and and_4 (and_4_out, and_3_out, DataIn[3]);
  xor xor_4 (DataOut[4], and_4_out, DataIn[4]);
  and and_5 (and_5_out, and_4_out, DataIn[4]);
  xor xor_5 (DataOut[5], and_5_out, DataIn[5]);
  and and_6 (and_6_out, and_5_out, DataIn[5]);
  xor xor_6 (DataOut[6], and_6_out, DataIn[6]);
  and and_7 (and_7_out, and_6_out, DataIn[6]);
  xor xor_7 (DataOut[7], and_7_out, DataIn[7]);
  and and_8 (and_8_out, and_7_out, DataIn[7]);
  xor xor_8 (DataOut[8], and_8_out, DataIn[8]);
  and and_9 (and_9_out, and_8_out, DataIn[8]);
  xor xor_9 (DataOut[9], and_9_out, DataIn[9]);
  and and_10 (and_10_out, and_9_out, DataIn[9]);
  xor xor_10 (DataOut[10], and_10_out, DataIn[10]);
  and and_11 (and_11_out, and_10_out, DataIn[10]);
  xor xor_11 (DataOut[11], and_11_out, DataIn[11]);
  and and_12 (and_12_out, and_11_out, DataIn[11]);
  xor xor_12 (DataOut[12], and_12_out, DataIn[12]);
  and and_13 (and_13_out, and_12_out, DataIn[12]);
  xor xor_13 (DataOut[13], and_13_out, DataIn[13]);
  and and_14 (and_14_out, and_13_out, DataIn[13]);
  xor xor_14 (DataOut[14], and_14_out, DataIn[14]);
  and and_15 (and_15_out, and_14_out, DataIn[14]);
  xor xor_15 (DataOut[15], and_15_out, DataIn[15]);
  and and_16 (Carry, and_15_out, DataIn[15]);
endmodule

module inc8OnOff (
  input  OnOff,
  input  [7:0] DataIn,
  output [7:0] DataOut,
  output Carry
);

  wire and_1_out, and_2_out, and_3_out, and_4_out, and_5_out, and_6_out, and_7_out, not_1_out;

  not not_1 (not_1_out, OnOff);
  assign DataOut[0] = not_1_out ? DataIn[0] : 1'bz;  // Controlled_Buffer controlled_buffer_1
  assign DataOut[0] = OnOff ? ~DataIn[0] : 1'bz;  // Controlled_Inverter controlled_inverter_1
  and and_1 (and_1_out, OnOff, DataIn[0]);
  xor xor_1 (DataOut[1], and_1_out, DataIn[1]);
  and and_2 (and_2_out, and_1_out, DataIn[1]);
  xor xor_2 (DataOut[2], and_2_out, DataIn[2]);
  and and_3 (and_3_out, and_2_out, DataIn[2]);
  xor xor_3 (DataOut[3], and_3_out, DataIn[3]);
  and and_4 (and_4_out, and_3_out, DataIn[3]);
  xor xor_4 (DataOut[4], and_4_out, DataIn[4]);
  and and_5 (and_5_out, and_4_out, DataIn[4]);
  xor xor_5 (DataOut[5], and_5_out, DataIn[5]);
  and and_6 (and_6_out, and_5_out, DataIn[5]);
  xor xor_6 (DataOut[6], and_6_out, DataIn[6]);
  and and_7 (and_7_out, and_6_out, DataIn[6]);
  xor xor_7 (DataOut[7], and_7_out, DataIn[7]);
  and and_8 (Carry, and_7_out, DataIn[7]);
endmodule

module dec16 (
  input  [15:0] DataIn,
  output [15:0] DataOut
);

  wire and_1_out, and_2_out, and_3_out, and_4_out, and_5_out, and_6_out, and_7_out, and_8_out, and_9_out,
       and_10_out, and_11_out, and_12_out, and_13_out, and_14_out, not_1_out, not_2_out, not_3_out,
       not_4_out, not_5_out, not_6_out, not_7_out, not_8_out, not_9_out, not_10_out, not_11_out, not_12_out,
       not_13_out, not_14_out;

  not not_1 (not_1_out, DataIn[1]);
  not not_2 (not_2_out, DataIn[2]);
  not not_3 (not_3_out, DataIn[3]);
  not not_4 (not_4_out, DataIn[4]);
  not not_5 (not_5_out, DataIn[5]);
  not not_6 (not_6_out, DataIn[6]);
  not not_7 (not_7_out, DataIn[7]);
  not not_8 (not_8_out, DataIn[8]);
  not not_9 (not_9_out, DataIn[9]);
  not not_10 (not_10_out, DataIn[10]);
  not not_11 (not_11_out, DataIn[11]);
  not not_12 (not_12_out, DataIn[12]);
  not not_13 (not_13_out, DataIn[13]);
  not not_14 (not_14_out, DataIn[14]);
  not not_15 (DataOut[0], DataIn[0]);
  xor xor_1 (DataOut[1], DataOut[0], DataIn[1]);
  and and_1 (and_1_out, DataOut[0], not_1_out);
  xor xor_2 (DataOut[2], and_1_out, DataIn[2]);
  and and_2 (and_2_out, and_1_out, not_2_out);
  xor xor_3 (DataOut[3], and_2_out, DataIn[3]);
  and and_3 (and_3_out, and_2_out, not_3_out);
  xor xor_4 (DataOut[4], and_3_out, DataIn[4]);
  and and_4 (and_4_out, and_3_out, not_4_out);
  xor xor_5 (DataOut[5], and_4_out, DataIn[5]);
  and and_5 (and_5_out, and_4_out, not_5_out);
  xor xor_6 (DataOut[6], and_5_out, DataIn[6]);
  and and_6 (and_6_out, and_5_out, not_6_out);
  xor xor_7 (DataOut[7], and_6_out, DataIn[7]);
  and and_7 (and_7_out, and_6_out, not_7_out);
  xor xor_8 (DataOut[8], and_7_out, DataIn[8]);
  and and_8 (and_8_out, and_7_out, not_8_out);
  xor xor_9 (DataOut[9], and_8_out, DataIn[9]);
  and and_9 (and_9_out, and_8_out, not_9_out);
  xor xor_10 (DataOut[10], and_9_out, DataIn[10]);
  and and_10 (and_10_out, and_9_out, not_10_out);
  xor xor_11 (DataOut[11], and_10_out, DataIn[11]);
  and and_11 (and_11_out, and_10_out, not_11_out);
  xor xor_12 (DataOut[12], and_11_out, DataIn[12]);
  and and_12 (and_12_out, and_11_out, not_12_out);
  xor xor_13 (DataOut[13], and_12_out, DataIn[13]);
  and and_13 (and_13_out, and_12_out, not_13_out);
  xor xor_14 (DataOut[14], and_13_out, DataIn[14]);
  and and_14 (and_14_out, and_13_out, not_14_out);
  xor xor_15 (DataOut[15], and_14_out, DataIn[15]);
endmodule
